// Logisim project CECS361_RISC_CPU_Design.circ as structural Verilog: 1 circuit, main circuit main
module main (
  input  CPU_Reset,
  input  in_2,
  input  in_3
);

  wire and_1_out, and_2_out, and_3_out, and_4_out, and_5_out, and_6_out, and_7_out, and_8_out, and_9_out,
       and_10_out, and_11_out, and_12_out, BT_Reg_Addr_out, clock_1_out, comparator_1_gt, comparator_2_gt,
       comparator_3_eq, comparator_3_lt, d_ff_1_q, decoder_1_out0, decoder_1_out1, decoder_1_out2,
       decoder_1_out3, decoder_1_out4, decoder_1_out5, decoder_1_out6, decoder_1_out7, decoder_1_out8,
       decoder_1_out9, decoder_2_out0, decoder_2_out1, decoder_2_out2, decoder_2_out3, decoder_2_out4,
       decoder_2_out5, decoder_2_out6, decoder_2_out7, LED_Reg_Addr_out, not_1_out, not_2_out, not_3_out,
       not_4_out, not_5_out, not_6_out, not_7_out, not_8_out, not_9_out, not_10_out, not_11_out, not_12_out,
       not_13_out, not_14_out, not_15_out, not_16_out, not_17_out, not_18_out, not_19_out, not_20_out,
       not_21_out, not_22_out, not_23_out, not_24_out, not_25_out, not_26_out, not_27_out, not_28_out,
       not_29_out, not_30_out, not_31_out, not_32_out, not_33_out, not_34_out, not_35_out, not_36_out,
       or_1_out, or_2_out, or_3_out, priority_encoder_2_out, RGB_Reg_Addr_out, Seg_0_Addr_out,
       Seg_1_Addr_out, Seg_2_Addr_out, Seg_3_Addr_out, Seg_4_Addr_out, Seg_5_Addr_out, Seg_6_Addr_out,
       Seg_7_Addr_out, SW_Reg_Addr_out, xor_1_out, xor_2_out;
  wire [2:0] demultiplexer_6_out0, demultiplexer_6_out1, demultiplexer_6_out2, demultiplexer_6_out3,
       demultiplexer_6_out4, demultiplexer_6_out5, demultiplexer_6_out6, demultiplexer_6_out7,
       demultiplexer_7_out3, demultiplexer_7_out4, demultiplexer_7_out5, demultiplexer_7_out6,
       demultiplexer_7_out7, multiplexer_4_out, multiplexer_5_out, multiplexer_6_out, multiplexer_8_out,
       rom_1_data, rom_1_data_2;
  wire [3:0] multiplexer_10_out, priority_encoder_1_out;
  wire [4:0] Right_out;
  wire [5:0] rom_1_data_4;
  wire [7:0] demultiplexer_9_out1;
  wire [15:0] adder_1_out, and_13_out, BT_Reg_q, demultiplexer_1_out0, demultiplexer_1_out1,
       demultiplexer_1_out2, demultiplexer_1_out3, demultiplexer_1_out4, demultiplexer_1_out5,
       demultiplexer_1_out6, demultiplexer_1_out7, demultiplexer_2_out0, demultiplexer_2_out1,
       demultiplexer_2_out2, demultiplexer_2_out3, demultiplexer_2_out4, demultiplexer_2_out5,
       demultiplexer_2_out6, demultiplexer_2_out7, demultiplexer_2_out8, demultiplexer_2_out9,
       demultiplexer_3_out1, demultiplexer_4_out3, demultiplexer_4_out4, demultiplexer_4_out5,
       demultiplexer_4_out6, demultiplexer_4_out7, demultiplexer_5_out2, demultiplexer_5_out3,
       demultiplexer_5_out4, demultiplexer_5_out5, demultiplexer_5_out6, demultiplexer_5_out7,
       demultiplexer_8_out0, demultiplexer_8_out1, demultiplexer_9_out0, demultiplexer_9_out2, LED_Reg_q,
       multiplexer_1_out, multiplexer_2_out, multiplexer_3_out, multiplexer_7_out, multiplexer_9_out,
       multiplexer_11_out, or_4_out, Program_Counter_q, R0_q, R1_q, R2_q, R3_q, R4_q, R5_q, R6_q, R7_q,
       ram_1_dout, RGB_p2, Seg0_q, Seg1_q, Seg2_q, Seg3_q, Seg4_q, Seg5_q, Seg6_q, Seg7_q, subtractor_1_out,
       SW_Reg_q, undriven;
  wire [15:8] demultiplexer_9_out1_2;
  wire [15:12] rom_1_data_3;

  Clock #(.phaseOffset(1)) clock_1 (.out(clock_1_out));
  xor xor_1 (xor_1_out, and_4_out, 1'b1);
  D_Flip_Flop d_ff_1 (.D(xor_1_out), .clk(clock_1_out), .Q(d_ff_1_q), .reset(and_5_out));  // open: Qn, preset
  RAM #(.dataWidth(16)) ram_1 (
    .addr(demultiplexer_9_out1), .we(in_3), .oe(in_2), .clk(clock_1_out), .din(demultiplexer_8_out0),
    .dout(ram_1_dout));
  Decoder #(.select(4)) decoder_1 (
    .out0(decoder_1_out0), .out1(decoder_1_out1), .out2(decoder_1_out2), .out3(decoder_1_out3),
    .out4(decoder_1_out4), .out5(decoder_1_out5), .out6(decoder_1_out6), .out7(decoder_1_out7),
    .out8(decoder_1_out8), .out9(decoder_1_out9), .sel(multiplexer_10_out), .en(and_12_out));  // open: out10, out11, out12, out13, out14, out15
  Decoder #(.select(3)) decoder_2 (
    .out0(decoder_2_out0), .out1(decoder_2_out1), .out2(decoder_2_out2), .out3(decoder_2_out3),
    .out4(decoder_2_out4), .out5(decoder_2_out5), .out6(decoder_2_out6), .out7(decoder_2_out7),
    .sel(multiplexer_8_out), .en(and_10_out));
  Multiplexer #(.width(16)) multiplexer_1 (
    .in0(SW_Reg_q), .in1(BT_Reg_q), .out(multiplexer_1_out), .sel(priority_encoder_2_out));
  Multiplexer #(.select(3), .width(16)) multiplexer_2 (
    .in0(R0_q), .in1(R1_q), .in2(R2_q), .in3(R3_q), .in4(R4_q), .in5(R5_q), .in6(R6_q), .in7(R7_q),
    .out(multiplexer_2_out), .sel(multiplexer_4_out));
  Multiplexer #(.select(3), .width(16)) multiplexer_3 (
    .in0(R0_q), .in1(R1_q), .in2(R2_q), .in3(R3_q), .in4(R4_q), .in5(R5_q), .in6(R6_q), .in7(R7_q),
    .out(multiplexer_3_out), .sel(multiplexer_5_out));
  Demultiplexer #(.select(3), .width(16)) demultiplexer_1 (
    .out0(demultiplexer_1_out0), .out1(demultiplexer_1_out1), .out2(demultiplexer_1_out2),
    .out3(demultiplexer_1_out3), .out4(demultiplexer_1_out4), .out5(demultiplexer_1_out5),
    .out6(demultiplexer_1_out6), .out7(demultiplexer_1_out7), .in(multiplexer_7_out), .sel(multiplexer_6_out));
  Demultiplexer #(.select(4), .width(16)) demultiplexer_2 (
    .out0(demultiplexer_2_out0), .out1(demultiplexer_2_out1), .out2(demultiplexer_2_out2),
    .out3(demultiplexer_2_out3), .out4(demultiplexer_2_out4), .out5(demultiplexer_2_out5),
    .out6(demultiplexer_2_out6), .out7(demultiplexer_2_out7), .out8(demultiplexer_2_out8),
    .out9(demultiplexer_2_out9), .in(multiplexer_9_out), .sel(priority_encoder_1_out));  // open: out10, out11, out12, out13, out14, out15
  Register #(.width(16)) R7 (
    .D(demultiplexer_1_out7), .en(decoder_2_out7), .clk(clock_1_out), .Q(R7_q), .clr(CPU_Reset));
  or or_1 (or_1_out, and_6_out, and_3_out, and_2_out, and_1_out);
  Demultiplexer #(.select(4), .width(16)) demultiplexer_3 (
    .out1(demultiplexer_3_out1), .in(multiplexer_1_out), .sel(rom_1_data_3));  // open: out0, out2, out3, out4, out5, out6, out7, out8, out9, out10, out11, out12, out13, out14, out15
  Counter #(.max('hffff), .width(16)) Program_Counter (
    .clr(CPU_Reset), .load(or_1_out), .up(1'b1), .count(d_ff_1_q), .clk(clock_1_out),
    .D({4'b0000, rom_1_data_2, rom_1_data, rom_1_data_4}), .Q(Program_Counter_q));  // open: carry
  Demultiplexer #(.select(4), .width(16)) demultiplexer_4 (
    .out3(demultiplexer_4_out3), .out4(demultiplexer_4_out4), .out5(demultiplexer_4_out5),
    .out6(demultiplexer_4_out6), .out7(demultiplexer_4_out7), .in(multiplexer_2_out), .sel(rom_1_data_3));  // open: out0, out1, out2, out8, out9, out10, out11, out12, out13, out14, out15
  and and_1 (and_1_out, comparator_3_lt, and_9_out);
  and and_2 (and_2_out, and_8_out, not_1_out);
  not not_1 (not_1_out, comparator_3_eq);
  and and_3 (and_3_out, comparator_3_eq, and_7_out);
  ROM #(.dataWidth(16)) rom_1 (
    .addr(Program_Counter_q[7:0]), .data({rom_1_data_3, rom_1_data, rom_1_data_2, rom_1_data_4}));
  Register #(.width(16)) R6 (
    .D(demultiplexer_1_out6), .en(decoder_2_out6), .clk(clock_1_out), .Q(R6_q), .clr(CPU_Reset));
  Multiplexer #(.select(4), .width(3)) multiplexer_4 (
    .in0(3'b000), .in1(3'b000), .in2(3'b000), .in3(demultiplexer_7_out3), .in4(demultiplexer_7_out4),
    .in5(demultiplexer_7_out5), .in6(demultiplexer_7_out6), .in7(demultiplexer_7_out7), .in8(3'b000),
    .in9(3'b000), .in10(3'b000), .in11(3'b000), .in12(3'b000), .in13(3'b000), .in14(3'b000), .in15(3'b000),
    .out(multiplexer_4_out));  // open: sel
  Demultiplexer #(.select(4), .width(16)) demultiplexer_5 (
    .out2(demultiplexer_5_out2), .out3(demultiplexer_5_out3), .out4(demultiplexer_5_out4),
    .out5(demultiplexer_5_out5), .out6(demultiplexer_5_out6), .out7(demultiplexer_5_out7),
    .in(multiplexer_3_out), .sel(rom_1_data_3));  // open: out0, out1, out8, out9, out10, out11, out12, out13, out14, out15
  and and_4 (and_4_out, rom_1_data_3[15], rom_1_data_3[14], not_2_out, not_4_out);
  not not_2 (not_2_out, rom_1_data_3[13]);
  and and_5 (and_5_out, rom_1_data_3[15], rom_1_data_3[14], not_3_out, rom_1_data_3[12]);
  not not_3 (not_3_out, rom_1_data_3[13]);
  not not_4 (not_4_out, rom_1_data_3[12]);
  Multiplexer #(.select(4), .width(3)) multiplexer_5 (
    .in0(3'b000), .in1(3'b000), .in2(demultiplexer_6_out2), .in3(demultiplexer_6_out3),
    .in4(demultiplexer_6_out4), .in5(demultiplexer_6_out5), .in6(demultiplexer_6_out6),
    .in7(demultiplexer_6_out7), .in8(3'b000), .in9(3'b000), .in10(3'b000), .in11(3'b000), .in12(3'b000),
    .in13(3'b000), .in14(3'b000), .in15(3'b000), .out(multiplexer_5_out));  // open: sel
  Register #(.width(16)) R5 (
    .D(demultiplexer_1_out5), .en(decoder_2_out5), .clk(clock_1_out), .Q(R5_q), .clr(CPU_Reset));
  and and_6 (and_6_out, rom_1_data_3[15], not_5_out, not_6_out, not_7_out);
  not not_5 (not_5_out, rom_1_data_3[14]);
  not not_6 (not_6_out, rom_1_data_3[13]);
  not not_7 (not_7_out, rom_1_data_3[12]);
  and and_7 (and_7_out, rom_1_data_3[15], not_8_out, not_9_out, rom_1_data_3[12]);
  not not_8 (not_8_out, rom_1_data_3[14]);
  not not_9 (not_9_out, rom_1_data_3[13]);
  Demultiplexer #(.select(4), .width(3)) demultiplexer_6 (
    .out0(demultiplexer_6_out0), .out1(demultiplexer_6_out1), .out2(demultiplexer_6_out2),
    .out3(demultiplexer_6_out3), .out4(demultiplexer_6_out4), .out5(demultiplexer_6_out5),
    .out6(demultiplexer_6_out6), .out7(demultiplexer_6_out7), .in(rom_1_data), .sel(rom_1_data_3));  // open: out8, out9, out10, out11, out12, out13, out14, out15
  and and_8 (and_8_out, rom_1_data_3[15], not_10_out, rom_1_data_3[13], not_11_out);
  and and_9 (and_9_out, rom_1_data_3[15], not_12_out, rom_1_data_3[13], rom_1_data_3[12]);
  not not_10 (not_10_out, rom_1_data_3[14]);
  not not_11 (not_11_out, rom_1_data_3[12]);
  not not_12 (not_12_out, rom_1_data_3[14]);
  Multiplexer #(.select(4), .width(3)) multiplexer_6 (
    .in0(demultiplexer_6_out0), .in1(demultiplexer_6_out1), .in2(3'b000), .in3(demultiplexer_6_out3),
    .in4(demultiplexer_6_out4), .in5(demultiplexer_6_out5), .in6(demultiplexer_6_out6),
    .in7(demultiplexer_6_out7), .in8(3'b000), .in9(3'b000), .in10(3'b000), .in11(3'b000), .in12(3'b000),
    .in13(3'b000), .in14(3'b000), .in15(3'b000), .out(multiplexer_6_out), .sel(rom_1_data_3));
  Multiplexer #(.select(4), .width(16)) multiplexer_7 (
    .in0(demultiplexer_9_out0), .in1(multiplexer_11_out), .in2({16{1'b0}}), .in3(adder_1_out),
    .in4(subtractor_1_out), .in5(and_13_out), .in6(or_4_out), .in7({16{1'b0}}), .in8({16{1'b0}}),
    .in9({16{1'b0}}), .in10({16{1'b0}}), .in11({16{1'b0}}), .in12({16{1'b0}}), .in13({16{1'b0}}),
    .in14({16{1'b0}}), .in15({16{1'b0}}), .out(multiplexer_7_out), .sel(rom_1_data_3));
  Multiplexer #(.select(4), .width(3)) multiplexer_8 (
    .in0(demultiplexer_6_out0), .in1(demultiplexer_6_out1), .in2(demultiplexer_6_out2), .in3(3'b000),
    .in4(3'b000), .in5(3'b000), .in6(3'b000), .in7(3'b000), .in8(3'b000), .in9(3'b000), .in10(3'b000),
    .in11(3'b000), .in12(3'b000), .in13(3'b000), .in14(3'b000), .in15(3'b000), .out(multiplexer_8_out),
    .sel(rom_1_data_3));
  Multiplexer #(.select(4), .width(16)) multiplexer_9 (
    .in0({16{1'b0}}), .in1({16{1'b0}}), .in2(demultiplexer_8_out1), .in3({16{1'b0}}), .in4({16{1'b0}}),
    .in5({16{1'b0}}), .in6({16{1'b0}}), .in7({16{1'b0}}), .in8({16{1'b0}}), .in9({16{1'b0}}),
    .in10({16{1'b0}}), .in11({16{1'b0}}), .in12({16{1'b0}}), .in13({16{1'b0}}), .in14({16{1'b0}}),
    .in15({16{1'b0}}), .out(multiplexer_9_out), .sel(rom_1_data_3));
  Multiplexer #(.select(4), .width(4)) multiplexer_10 (
    .in0(4'b0000), .in1(4'b0000), .in2(priority_encoder_1_out), .in3(4'b0000), .in4(4'b0000), .in5(4'b0000),
    .in6(4'b0000), .in7(4'b0000), .in8(4'b0000), .in9(4'b0000), .in10(4'b0000), .in11(4'b0000),
    .in12(4'b0000), .in13(4'b0000), .in14(4'b0000), .in15(4'b0000), .out(multiplexer_10_out),
    .sel(rom_1_data_3));
  Multiplexer #(.width(16)) multiplexer_11 (
    .in0(ram_1_dout), .in1(demultiplexer_3_out1), .out(multiplexer_11_out), .sel(comparator_1_gt));
  Register #(.width(16)) R4 (
    .D(demultiplexer_1_out4), .en(decoder_2_out4), .clk(clock_1_out), .Q(R4_q), .clr(CPU_Reset));
  Demultiplexer #(.select(4), .width(3)) demultiplexer_7 (
    .out3(demultiplexer_7_out3), .out4(demultiplexer_7_out4), .out5(demultiplexer_7_out5),
    .out6(demultiplexer_7_out6), .out7(demultiplexer_7_out7), .in(rom_1_data_2), .sel(rom_1_data_3));  // open: out0, out1, out2, out8, out9, out10, out11, out12, out13, out14, out15
  Demultiplexer #(.width(16)) demultiplexer_8 (
    .out0(demultiplexer_8_out0), .out1(demultiplexer_8_out1), .in(demultiplexer_5_out2), .sel(comparator_2_gt));
  not not_13 (not_13_out, rom_1_data_3[15]);
  not not_14 (not_14_out, rom_1_data_3[13]);
  or or_2 (or_2_out, rom_1_data_3[14], not_14_out, rom_1_data_3[12]);
  and and_10 (and_10_out, not_13_out, or_2_out);
  not not_15 (not_15_out, rom_1_data_3[15]);
  not not_16 (not_16_out, rom_1_data_3[14]);
  and and_11 (and_11_out, not_15_out, not_16_out);
  and and_12 (and_12_out, and_11_out, xor_2_out);
  Register #(.width(16)) R3 (
    .D(demultiplexer_1_out3), .en(decoder_2_out3), .clk(clock_1_out), .Q(R3_q), .clr(CPU_Reset));
  xor xor_2 (xor_2_out, rom_1_data_3[13], rom_1_data_3[12]);
  Comparator #(.width(16)) comparator_1 (
    .a({demultiplexer_9_out1_2, demultiplexer_9_out1}), .b(16'h33), .gt(comparator_1_gt));  // open: eq, lt
  Comparator #(.width(16)) comparator_2 (.a(demultiplexer_9_out2), .b(16'h33), .gt(comparator_2_gt));  // open: eq, lt
  Demultiplexer #(.select(4), .width(16)) demultiplexer_9 (
    .out0(demultiplexer_9_out0), .out1({demultiplexer_9_out1_2, demultiplexer_9_out1}),
    .out2(demultiplexer_9_out2), .in({{10{1'b0}}, rom_1_data_4}), .sel(rom_1_data_3));  // open: out3, out4, out5, out6, out7, out8, out9, out10, out11, out12, out13, out14, out15
  not not_17 (not_17_out, rom_1_data_4[3]);
  not not_18 (not_18_out, rom_1_data_4[1]);
  and BT_Reg_Addr (BT_Reg_Addr_out, rom_1_data_4[5], rom_1_data_4[4], not_17_out, rom_1_data_4[2], not_18_out, not_19_out);
  Register #(.width(16)) R2 (
    .D(demultiplexer_1_out2), .en(decoder_2_out2), .clk(clock_1_out), .Q(R2_q), .clr(CPU_Reset));
  not not_19 (not_19_out, rom_1_data_4[0]);
  not not_20 (not_20_out, rom_1_data_4[3]);
  not not_21 (not_21_out, rom_1_data_4[1]);
  and SW_Reg_Addr (SW_Reg_Addr_out, rom_1_data_4[5], rom_1_data_4[4], not_20_out, rom_1_data_4[2], not_21_out, rom_1_data_4[0]);
  not not_22 (not_22_out, rom_1_data_4[3]);
  and LED_Reg_Addr (LED_Reg_Addr_out, rom_1_data_4[5], rom_1_data_4[4], not_22_out, rom_1_data_4[2], rom_1_data_4[1], not_23_out);
  not not_23 (not_23_out, rom_1_data_4[0]);
  not not_24 (not_24_out, rom_1_data_4[3]);
  and RGB_Reg_Addr (RGB_Reg_Addr_out, rom_1_data_4[5], rom_1_data_4[4], not_24_out, rom_1_data_4[2], rom_1_data_4[1], rom_1_data_4[0]);
  not not_25 (not_25_out, rom_1_data_4[0]);
  not not_26 (not_26_out, rom_1_data_4[1]);
  not not_27 (not_27_out, rom_1_data_4[2]);
  and Seg_7_Addr (Seg_7_Addr_out, rom_1_data_4[5], rom_1_data_4[4], rom_1_data_4[3], not_27_out, not_26_out, not_25_out);
  Register #(.width(16)) R1 (
    .D(demultiplexer_1_out1), .en(decoder_2_out1), .clk(clock_1_out), .Q(R1_q), .clr(CPU_Reset));
  not not_28 (not_28_out, rom_1_data_4[1]);
  not not_29 (not_29_out, rom_1_data_4[2]);
  and Seg_6_Addr (Seg_6_Addr_out, rom_1_data_4[5], rom_1_data_4[4], rom_1_data_4[3], not_29_out, not_28_out, rom_1_data_4[0]);
  not not_30 (not_30_out, rom_1_data_4[0]);
  not not_31 (not_31_out, rom_1_data_4[2]);
  and Seg_5_Addr (Seg_5_Addr_out, rom_1_data_4[5], rom_1_data_4[4], rom_1_data_4[3], not_31_out, rom_1_data_4[1], not_30_out);
  not not_32 (not_32_out, rom_1_data_4[2]);
  and Seg_4_Addr (Seg_4_Addr_out, rom_1_data_4[5], rom_1_data_4[4], rom_1_data_4[3], not_32_out, rom_1_data_4[1], rom_1_data_4[0]);
  not not_33 (not_33_out, rom_1_data_4[1]);
  and Seg_3_Addr (Seg_3_Addr_out, rom_1_data_4[5], rom_1_data_4[4], rom_1_data_4[3], rom_1_data_4[2], not_33_out, not_34_out);
  Button Left (.out(Right_out[2]));
  not not_34 (not_34_out, rom_1_data_4[0]);
  not not_35 (not_35_out, rom_1_data_4[1]);
  and Seg_2_Addr (Seg_2_Addr_out, rom_1_data_4[5], rom_1_data_4[4], rom_1_data_4[3], rom_1_data_4[2], not_35_out, rom_1_data_4[0]);
  Button Up (.out(Right_out[3]));
  Button Enter (.out(Right_out[4]));
  Button Down (.out(Right_out[1]));
  and Seg_1_Addr (Seg_1_Addr_out, rom_1_data_4[5], rom_1_data_4[4], rom_1_data_4[3], rom_1_data_4[2], rom_1_data_4[1], not_36_out);
  Register #(.width(16)) R0 (
    .D(demultiplexer_1_out0), .en(decoder_2_out0), .clk(clock_1_out), .Q(R0_q), .clr(CPU_Reset));
  // DipSwitch #(.number(16)) dipswitch_1: pin names not known
  Button Right (.out(Right_out[0]));
  not not_36 (not_36_out, rom_1_data_4[0]);
  and Seg_0_Addr (Seg_0_Addr_out, rom_1_data_4[5], rom_1_data_4[4], rom_1_data_4[3], rom_1_data_4[2], rom_1_data_4[1], rom_1_data_4[0]);
  or or_3 (or_3_out, LED_Reg_Addr_out, RGB_Reg_Addr_out, Seg_7_Addr_out, Seg_6_Addr_out, Seg_5_Addr_out, Seg_4_Addr_out, Seg_3_Addr_out, Seg_2_Addr_out, Seg_1_Addr_out, Seg_0_Addr_out);
  Priority_Encoder #(.select(4)) priority_encoder_1 (
    .in0(Seg_0_Addr_out), .in1(Seg_1_Addr_out), .in2(Seg_2_Addr_out), .in3(Seg_3_Addr_out),
    .in4(Seg_4_Addr_out), .in5(Seg_5_Addr_out), .in6(Seg_6_Addr_out), .in7(Seg_7_Addr_out),
    .in8(RGB_Reg_Addr_out), .in9(LED_Reg_Addr_out), .in10(1'b0), .in11(1'b0), .in12(1'b0), .in13(1'b0),
    .in14(1'b0), .in15(1'b0), .out(priority_encoder_1_out), .en_in(or_3_out));  // open: gs, en_out
  Priority_Encoder #(.select(1)) priority_encoder_2 (
    .in0(SW_Reg_Addr_out), .in1(BT_Reg_Addr_out), .out(priority_encoder_2_out), .en_in(BT_Reg_Addr_out));  // open: gs, en_out
  Register #(.width(16)) BT_Reg (
    .D({{11{1'b0}}, Right_out}), .en(1'b1), .clk(clock_1_out), .Q(BT_Reg_q), .clr(CPU_Reset));
  Register #(.width(16)) SW_Reg (.D(undriven), .en(1'b1), .clk(clock_1_out), .Q(SW_Reg_q), .clr(CPU_Reset));
  _7_Segment_Display u_7_segment_display_1 (
    .g(Seg7_q[6]), .f(Seg7_q[5]), .a(Seg7_q[0]), .b(Seg7_q[1]), .e(Seg7_q[4]), .d(Seg7_q[3]), .c(Seg7_q[2]));  // open: dp
  Register #(.width(16)) LED_Reg (
    .D(demultiplexer_2_out9), .en(decoder_1_out9), .clk(clock_1_out), .Q(LED_Reg_q), .clr(CPU_Reset));
  // RGBLED RGB: pin names not known; wires that end beside it: RGB_p2[2], RGB_p2[0], RGB_p2[1]
  _7_Segment_Display u_7_segment_display_2 (
    .g(Seg6_q[6]), .f(Seg6_q[5]), .a(Seg6_q[0]), .b(Seg6_q[1]), .e(Seg6_q[4]), .d(Seg6_q[3]), .c(Seg6_q[2]));  // open: dp
  _7_Segment_Display u_7_segment_display_3 (
    .g(Seg5_q[6]), .f(Seg5_q[5]), .a(Seg5_q[0]), .b(Seg5_q[1]), .e(Seg5_q[4]), .d(Seg5_q[3]), .c(Seg5_q[2]));  // open: dp
  // LedBar #(.inputtype("row"), .matrixcols(16)) ledbar_1: pin names not known; wires that end beside it: LED_Reg_q
  _7_Segment_Display u_7_segment_display_4 (
    .g(Seg4_q[6]), .f(Seg4_q[5]), .a(Seg4_q[0]), .b(Seg4_q[1]), .e(Seg4_q[4]), .d(Seg4_q[3]), .c(Seg4_q[2]));  // open: dp
  _7_Segment_Display u_7_segment_display_5 (
    .g(Seg3_q[6]), .f(Seg3_q[5]), .a(Seg3_q[0]), .b(Seg3_q[1]), .e(Seg3_q[4]), .d(Seg3_q[3]), .c(Seg3_q[2]));  // open: dp
  Register #(.width(16)) RGB_Reg (
    .D(demultiplexer_2_out8), .en(decoder_1_out8), .clk(clock_1_out), .Q(RGB_p2), .clr(CPU_Reset));
  _7_Segment_Display u_7_segment_display_6 (
    .g(Seg2_q[6]), .f(Seg2_q[5]), .a(Seg2_q[0]), .b(Seg2_q[1]), .e(Seg2_q[4]), .d(Seg2_q[3]), .c(Seg2_q[2]));  // open: dp
  Register #(.width(16)) Seg7 (
    .D(demultiplexer_2_out7), .en(decoder_1_out7), .clk(clock_1_out), .Q(Seg7_q), .clr(CPU_Reset));
  _7_Segment_Display u_7_segment_display_7 (
    .g(Seg1_q[6]), .f(Seg1_q[5]), .a(Seg1_q[0]), .b(Seg1_q[1]), .e(Seg1_q[4]), .d(Seg1_q[3]), .c(Seg1_q[2]));  // open: dp
  _7_Segment_Display u_7_segment_display_8 (
    .g(Seg0_q[6]), .f(Seg0_q[5]), .a(Seg0_q[0]), .b(Seg0_q[1]), .e(Seg0_q[4]), .d(Seg0_q[3]), .c(Seg0_q[2]));  // open: dp
  Register #(.width(16)) Seg6 (
    .D(demultiplexer_2_out6), .en(decoder_1_out6), .clk(clock_1_out), .Q(Seg6_q), .clr(CPU_Reset));
  Register #(.width(16)) Seg5 (
    .D(demultiplexer_2_out5), .en(decoder_1_out5), .clk(clock_1_out), .Q(Seg5_q), .clr(CPU_Reset));
  Register #(.width(16)) Seg4 (
    .D(demultiplexer_2_out4), .en(decoder_1_out4), .clk(clock_1_out), .Q(Seg4_q), .clr(CPU_Reset));
  Register #(.width(16)) Seg3 (
    .D(demultiplexer_2_out3), .en(decoder_1_out3), .clk(clock_1_out), .Q(Seg3_q), .clr(CPU_Reset));
  Register #(.width(16)) Seg2 (
    .D(demultiplexer_2_out2), .en(decoder_1_out2), .clk(clock_1_out), .Q(Seg2_q), .clr(CPU_Reset));
  Register #(.width(16)) Seg1 (
    .D(demultiplexer_2_out1), .en(decoder_1_out1), .clk(clock_1_out), .Q(Seg1_q), .clr(CPU_Reset));
  Register #(.width(16)) Seg0 (
    .D(demultiplexer_2_out0), .en(decoder_1_out0), .clk(clock_1_out), .Q(Seg0_q), .clr(CPU_Reset));
  Adder #(.width(16)) adder_1 (
    .a(demultiplexer_5_out3), .b(demultiplexer_4_out3), .out(adder_1_out));  // open: cin, cout
  Subtractor #(.width(16)) subtractor_1 (
    .a(demultiplexer_5_out4), .b(demultiplexer_4_out4), .out(subtractor_1_out));  // open: bin, bout
  assign and_13_out = demultiplexer_5_out5 & demultiplexer_4_out5;  // AND_Gate and_13, 16 bits wide
  assign or_4_out = demultiplexer_5_out6 | demultiplexer_4_out6;  // OR_Gate or_4, 16 bits wide
  Comparator #(.width(16)) comparator_3 (
    .a(demultiplexer_5_out7), .b(demultiplexer_4_out7), .eq(comparator_3_eq), .lt(comparator_3_lt));  // open: gt

  // Notes on the sheet:
  //   contents of rom_1 (hex, n*v repeats v):
  //   3f 200 203f 223f 63f 2601 4200 401 2437 c000 1634 2636 800a
endmodule
