// Logisim project CECS361_RISC_CPU_Design_V3.circ as structural Verilog: 3 circuits, main circuit main
module main (
  input  CPU_Reset
);

  wire and_1_out, and_2_out, and_3_out, and_4_out, and_5_out, and_6_out, and_7_out, and_8_out, and_9_out,
       and_10_out, and_11_out, and_12_out, and_18_out, and_20_out, and_21_out, and_22_out, and_23_out,
       and_25_out, and_26_out, and_27_out, and_28_out, and_29_out, and_30_out, and_31_out, and_32_out,
       and_33_out, and_34_out, and_35_out, and_36_out, and_37_out, and_38_out, and_39_out, and_40_out,
       and_41_out, and_42_out, and_43_out, and_44_out, and_45_out, and_46_out, and_47_out, and_48_out,
       BT_Reg_Addr_out, button_1_out, clock_1_out, comparator_1_gt, comparator_2_gt, comparator_3_eq,
       comparator_3_lt, d_ff_1_q, d_ff_2_q, d_ff_2_qn, d_ff_3_q, decoder_1_out0, decoder_1_out1,
       decoder_1_out2, decoder_1_out3, decoder_1_out4, decoder_1_out5, decoder_1_out6, decoder_1_out7,
       decoder_1_out8, decoder_1_out9, decoder_2_out0, decoder_2_out1, decoder_2_out2, decoder_2_out3,
       decoder_2_out4, decoder_2_out5, decoder_2_out6, decoder_2_out7, F_Seg4_out, HALT_out, I_Seg4_out,
       JMP_out, JN_out, JNZ_out, JZ_out, L_Seg4_out, LED_Reg_Addr_out, multiplexer_12_out, N_flag_reg_q,
       NOP_out, not_1_out, not_2_out, not_3_out, not_4_out, not_5_out, not_6_out, not_7_out, not_8_out,
       not_9_out, not_10_out, not_11_out, not_12_out, not_13_out, not_14_out, not_15_out, not_16_out,
       not_17_out, not_18_out, not_19_out, not_20_out, not_21_out, not_22_out, not_23_out, not_24_out,
       not_25_out, not_26_out, not_27_out, not_28_out, not_29_out, not_30_out, not_31_out, not_32_out,
       not_33_out, not_34_out, not_35_out, not_36_out, not_37_out, not_38_out, not_39_out, not_40_out,
       not_41_out, not_42_out, not_43_out, not_44_out, not_45_out, not_46_out, not_47_out, not_48_out,
       not_49_out, not_50_out, not_51_out, not_52_out, not_53_out, not_54_out, not_55_out, not_56_out,
       not_57_out, not_58_out, not_59_out, not_60_out, not_61_out, not_62_out, not_63_out, not_64_out,
       not_65_out, not_66_out, not_67_out, not_68_out, not_69_out, not_70_out, not_71_out, not_72_out,
       not_73_out, not_74_out, not_75_out, not_76_out, not_77_out, not_78_out, not_79_out, not_80_out,
       not_81_out, not_82_out, not_83_out, not_84_out, not_85_out, not_86_out, not_87_out, not_88_out,
       not_89_out, not_90_out, not_91_out, not_92_out, not_93_out, not_94_out, not_95_out, not_96_out,
       not_97_out, not_98_out, not_99_out, not_100_out, not_101_out, not_102_out, not_103_out, not_104_out,
       not_105_out, not_106_out, not_107_out, not_108_out, not_109_out, not_110_out, not_111_out,
       not_112_out, not_113_out, not_114_out, not_115_out, not_116_out, not_117_out, not_118_out,
       not_119_out, not_120_out, not_121_out, not_122_out, not_123_out, not_124_out, not_125_out,
       not_126_out, not_127_out, not_128_out, not_129_out, not_130_out, not_131_out, not_132_out,
       not_133_out, not_134_out, not_135_out, not_136_out, not_137_out, not_138_out, not_139_out,
       not_140_out, not_141_out, not_142_out, not_143_out, not_144_out, not_145_out, not_146_out,
       not_147_out, not_148_out, not_149_out, not_150_out, not_151_out, not_152_out, not_153_out,
       not_154_out, not_155_out, not_156_out, not_157_out, not_158_out, not_159_out, not_160_out,
       not_161_out, not_162_out, not_163_out, not_164_out, not_165_out, not_166_out, not_167_out,
       not_168_out, not_169_out, not_170_out, not_171_out, not_172_out, not_173_out, not_174_out,
       not_175_out, not_176_out, not_177_out, not_178_out, not_179_out, not_180_out, not_181_out,
       not_182_out, not_183_out, not_184_out, not_185_out, not_186_out, not_187_out, not_188_out,
       not_189_out, not_190_out, not_191_out, not_192_out, not_193_out, not_194_out, not_195_out,
       not_196_out, not_197_out, not_198_out, not_199_out, not_200_out, not_201_out, not_202_out,
       not_203_out, not_204_out, not_205_out, not_206_out, not_207_out, not_208_out, not_209_out,
       not_210_out, not_211_out, not_212_out, not_213_out, not_214_out, not_215_out, not_216_out,
       not_217_out, not_218_out, not_219_out, not_220_out, not_221_out, not_222_out, not_223_out,
       not_224_out, not_225_out, not_226_out, not_227_out, not_228_out, not_229_out, not_230_out,
       not_231_out, not_232_out, not_233_out, not_234_out, not_235_out, not_236_out, not_237_out,
       not_238_out, not_239_out, not_240_out, not_241_out, not_242_out, not_243_out, not_244_out,
       not_245_out, not_246_out, not_247_out, or_1_out, or_2_out, or_3_out, or_4_out, or_5_out, or_7_out,
       or_9_out, or_10_out, or_11_out, or_13_out, or_14_out, or_15_out, or_16_out, or_17_out, or_18_out,
       P_Seg4_out, priority_encoder_2_out, priority_encoder_3_p2, priority_encoder_3_p3,
       priority_encoder_3_p4, priority_encoder_3_p5, priority_encoder_3_p6, priority_encoder_3_p7,
       priority_encoder_4_p3, priority_encoder_4_p4, RGB_Reg_Addr_out, Seg_0_Addr_out, Seg_1_Addr_out,
       Seg_2_Addr_out, Seg_3_Addr_out, Seg_4_Addr_out, Seg_5_Addr_out, Seg_6_Addr_out, Seg_7_Addr_out,
       SW_Reg_Addr_out, xor_1_out, Z_flag_reg_q;
  wire [2:0] demultiplexer_6_out0, demultiplexer_6_out1, demultiplexer_6_out2, demultiplexer_6_out3,
       demultiplexer_6_out4, demultiplexer_6_out5, demultiplexer_6_out6, demultiplexer_6_out7,
       demultiplexer_7_out0, demultiplexer_7_out3, demultiplexer_7_out4, demultiplexer_7_out5,
       demultiplexer_7_out6, demultiplexer_7_out7, multiplexer_4_out, multiplexer_5_out, multiplexer_6_out,
       multiplexer_8_out, priority_encoder_3_p1, rom_1_data, rom_1_data_2;
  wire [3:0] multiplexer_10_out, multiplexer_14_out, priority_encoder_1_out;
  wire [4:0] Right_out;
  wire [5:0] rom_1_data_4;
  wire [7:0] multiplexer_13_out;
  wire [15:0] adder_1_out, and_24_out, BT_Reg_q, demultiplexer_1_out0, demultiplexer_1_out1,
       demultiplexer_1_out2, demultiplexer_1_out3, demultiplexer_1_out4, demultiplexer_1_out5,
       demultiplexer_1_out6, demultiplexer_1_out7, demultiplexer_2_out0, demultiplexer_2_out1,
       demultiplexer_2_out2, demultiplexer_2_out3, demultiplexer_2_out4, demultiplexer_2_out5,
       demultiplexer_2_out6, demultiplexer_2_out7, demultiplexer_2_out8, demultiplexer_2_out9,
       demultiplexer_3_out1, demultiplexer_4_out3, demultiplexer_4_out4, demultiplexer_4_out5,
       demultiplexer_4_out6, demultiplexer_4_out7, demultiplexer_5_out2, demultiplexer_5_out3,
       demultiplexer_5_out4, demultiplexer_5_out5, demultiplexer_5_out6, demultiplexer_5_out7,
       demultiplexer_8_out0, demultiplexer_8_out1, demultiplexer_9_out0, demultiplexer_9_out1,
       demultiplexer_9_out2, LED_Reg_q, multiplexer_1_out, multiplexer_2_out, multiplexer_3_out,
       multiplexer_7_out, multiplexer_9_out, multiplexer_11_out, multiplexer_15_out, multiplexer_16_out,
       multiplexer_17_out, multiplexer_18_out, multiplexer_19_out, multiplexer_20_out, multiplexer_21_out,
       multiplexer_22_out, multiplexer_23_out, or_6_out, or_12_out, Program_Counter_q, R0_q, R1_q, R2_q,
       R3_q, R4_q, R5_q, R6_q, R7_q, ram_1_dout, RGB_p2, Seg0_Decoder_a_2, Seg0_q, Seg1_Decoder_a_2, Seg1_q,
       Seg2_Decoder_a_2, Seg2_q, Seg3_Decoder_a_2, Seg3_q, Seg4_Decoder_a_2, Seg4_q, Seg5_Decoder_a_2,
       Seg5_q, Seg6_Decoder_a_2, Seg6_q, Seg7_Decoder_a_2, Seg7_q, subtractor_1_out, SW_Reg_q, undriven;
  wire [15:8] multiplexer_13_out_2;
  wire [15:12] rom_1_data_3;

  Button button_1 (.out(button_1_out));
  Clock #(.phaseOffset(1)) clock_1 (.out(clock_1_out));
  D_Flip_Flop d_ff_1 (.D(d_ff_2_qn), .clk(clock_1_out), .Q(d_ff_1_q), .reset(not_2_out));  // open: Qn, preset
  and and_1 (and_1_out, not_1_out, and_8_out);
  not not_1 (not_1_out, comparator_1_gt);
  or or_1 (or_1_out, and_1_out, NOP_out);
  not not_2 (not_2_out, or_1_out);
  and and_2 (and_2_out, or_1_out, not_3_out);
  not not_3 (not_3_out, d_ff_1_q);
  D_Flip_Flop d_ff_2 (.D(1'b1), .clk(clock_1_out), .Q(d_ff_2_q), .Qn(d_ff_2_qn), .preset(d_ff_1_q), .reset(or_2_out));
  or or_2 (or_2_out, HALT_out, and_2_out);
  and and_3 (and_3_out, and_7_out, not_4_out);
  not not_4 (not_4_out, comparator_2_gt);
  RAM #(.dataWidth(16), .readbehav("war")) ram_1 (
    .addr(multiplexer_13_out), .we(and_3_out), .oe(1'b1), .clk(clock_1_out), .din(demultiplexer_8_out0),
    .dout(ram_1_dout));
  Decoder #(.select(4)) decoder_1 (
    .out0(decoder_1_out0), .out1(decoder_1_out1), .out2(decoder_1_out2), .out3(decoder_1_out3),
    .out4(decoder_1_out4), .out5(decoder_1_out5), .out6(decoder_1_out6), .out7(decoder_1_out7),
    .out8(decoder_1_out8), .out9(decoder_1_out9), .sel(multiplexer_10_out), .en(and_12_out));  // open: out10, out11, out12, out13, out14, out15
  Decoder #(.select(3)) decoder_2 (
    .out0(decoder_2_out0), .out1(decoder_2_out1), .out2(decoder_2_out2), .out3(decoder_2_out3),
    .out4(decoder_2_out4), .out5(decoder_2_out5), .out6(decoder_2_out6), .out7(decoder_2_out7),
    .sel(multiplexer_8_out), .en(multiplexer_12_out));
  Multiplexer #(.width(16)) multiplexer_1 (
    .in0(SW_Reg_q), .in1(BT_Reg_q), .out(multiplexer_1_out), .sel(priority_encoder_2_out));
  Multiplexer #(.select(3), .width(16)) multiplexer_2 (
    .in0(R0_q), .in1(R1_q), .in2(R2_q), .in3(R3_q), .in4(R4_q), .in5(R5_q), .in6(R6_q), .in7(R7_q),
    .out(multiplexer_2_out), .sel(multiplexer_4_out));
  Multiplexer #(.select(3), .width(16)) multiplexer_3 (
    .in0(R0_q), .in1(R1_q), .in2(R2_q), .in3(R3_q), .in4(R4_q), .in5(R5_q), .in6(R6_q), .in7(R7_q),
    .out(multiplexer_3_out), .sel(multiplexer_5_out));
  Demultiplexer #(.select(3), .width(16)) demultiplexer_1 (
    .out0(demultiplexer_1_out0), .out1(demultiplexer_1_out1), .out2(demultiplexer_1_out2),
    .out3(demultiplexer_1_out3), .out4(demultiplexer_1_out4), .out5(demultiplexer_1_out5),
    .out6(demultiplexer_1_out6), .out7(demultiplexer_1_out7), .in(multiplexer_7_out), .sel(multiplexer_6_out));
  Demultiplexer #(.select(4), .width(16)) demultiplexer_2 (
    .out0(demultiplexer_2_out0), .out1(demultiplexer_2_out1), .out2(demultiplexer_2_out2),
    .out3(demultiplexer_2_out3), .out4(demultiplexer_2_out4), .out5(demultiplexer_2_out5),
    .out6(demultiplexer_2_out6), .out7(demultiplexer_2_out7), .out8(demultiplexer_2_out8),
    .out9(demultiplexer_2_out9), .in(multiplexer_9_out), .sel(priority_encoder_1_out));  // open: out10, out11, out12, out13, out14, out15
  Register #(.width(16)) R7 (
    .D(demultiplexer_1_out7), .en(decoder_2_out7), .clk(clock_1_out), .Q(R7_q), .clr(CPU_Reset));
  or or_3 (or_3_out, JMP_out, and_6_out, and_5_out, and_4_out);
  Demultiplexer #(.select(4), .width(16)) demultiplexer_3 (
    .out1(demultiplexer_3_out1), .in(multiplexer_1_out), .sel(rom_1_data_3));  // open: out0, out2, out3, out4, out5, out6, out7, out8, out9, out10, out11, out12, out13, out14, out15
  Counter #(.max('hffff), .width(16)) Program_Counter (
    .clr(CPU_Reset), .load(or_3_out), .up(1'b1), .count(d_ff_2_q), .clk(clock_1_out),
    .D({4'b0000, rom_1_data_2, rom_1_data, rom_1_data_4}), .Q(Program_Counter_q));  // open: carry
  Demultiplexer #(.select(4), .width(16)) demultiplexer_4 (
    .out3(demultiplexer_4_out3), .out4(demultiplexer_4_out4), .out5(demultiplexer_4_out5),
    .out6(demultiplexer_4_out6), .out7(demultiplexer_4_out7), .in(multiplexer_2_out), .sel(rom_1_data_3));  // open: out0, out1, out2, out8, out9, out10, out11, out12, out13, out14, out15
  ROM #(.addrWidth(16), .dataWidth(16)) rom_1 (
    .addr(Program_Counter_q), .data({rom_1_data_3, rom_1_data_2, rom_1_data, rom_1_data_4}));
  and and_4 (and_4_out, N_flag_reg_q, JN_out);
  and and_5 (and_5_out, JNZ_out, not_5_out);
  not not_5 (not_5_out, Z_flag_reg_q);
  and and_6 (and_6_out, Z_flag_reg_q, JZ_out);
  Register #(.width(16)) R6 (
    .D(demultiplexer_1_out6), .en(decoder_2_out6), .clk(clock_1_out), .Q(R6_q), .clr(CPU_Reset));
  Multiplexer #(.select(4), .width(3)) multiplexer_4 (
    .in0(3'b000), .in1(3'b000), .in2(3'b000), .in3(demultiplexer_7_out3), .in4(demultiplexer_7_out4),
    .in5(demultiplexer_7_out5), .in6(demultiplexer_7_out6), .in7(demultiplexer_7_out7), .in8(3'b000),
    .in9(3'b000), .in10(3'b000), .in11(3'b000), .in12(3'b000), .in13(3'b000), .in14(3'b000), .in15(3'b000),
    .out(multiplexer_4_out));  // open: sel
  not not_6 (not_6_out, rom_1_data_3[15]);
  Demultiplexer #(.select(4), .width(16)) demultiplexer_5 (
    .out2(demultiplexer_5_out2), .out3(demultiplexer_5_out3), .out4(demultiplexer_5_out4),
    .out5(demultiplexer_5_out5), .out6(demultiplexer_5_out6), .out7(demultiplexer_5_out7),
    .in(multiplexer_3_out), .sel(rom_1_data_3));  // open: out0, out1, out8, out9, out10, out11, out12, out13, out14, out15
  not not_7 (not_7_out, rom_1_data_3[12]);
  not not_8 (not_8_out, rom_1_data_3[14]);
  not not_9 (not_9_out, rom_1_data_3[14]);
  not not_10 (not_10_out, rom_1_data_3[15]);
  and and_7 (and_7_out, not_6_out, not_8_out, rom_1_data_3[13], not_7_out);
  and NOP (NOP_out, rom_1_data_3[15], rom_1_data_3[14], not_11_out, not_14_out);
  not not_11 (not_11_out, rom_1_data_3[13]);
  not not_12 (not_12_out, rom_1_data_3[13]);
  and and_8 (and_8_out, not_10_out, not_9_out, not_12_out, rom_1_data_3[12]);
  and HALT (HALT_out, rom_1_data_3[15], rom_1_data_3[14], not_13_out, rom_1_data_3[12]);
  not not_13 (not_13_out, rom_1_data_3[13]);
  not not_14 (not_14_out, rom_1_data_3[12]);
  Multiplexer #(.select(4), .width(3)) multiplexer_5 (
    .in0(3'b000), .in1(3'b000), .in2(demultiplexer_6_out2), .in3(demultiplexer_6_out3),
    .in4(demultiplexer_6_out4), .in5(demultiplexer_6_out5), .in6(demultiplexer_6_out6),
    .in7(demultiplexer_6_out7), .in8(3'b000), .in9(3'b000), .in10(3'b000), .in11(3'b000), .in12(3'b000),
    .in13(3'b000), .in14(3'b000), .in15(3'b000), .out(multiplexer_5_out));  // open: sel
  Register #(.width(16)) R5 (
    .D(demultiplexer_1_out5), .en(decoder_2_out5), .clk(clock_1_out), .Q(R5_q), .clr(CPU_Reset));
  and JMP (JMP_out, rom_1_data_3[15], not_15_out, not_16_out, not_17_out);
  not not_15 (not_15_out, rom_1_data_3[14]);
  not not_16 (not_16_out, rom_1_data_3[13]);
  not not_17 (not_17_out, rom_1_data_3[12]);
  and JZ (JZ_out, rom_1_data_3[15], not_18_out, not_19_out, rom_1_data_3[12]);
  not not_18 (not_18_out, rom_1_data_3[14]);
  not not_19 (not_19_out, rom_1_data_3[13]);
  Demultiplexer #(.select(4), .width(3)) demultiplexer_6 (
    .out0(demultiplexer_6_out0), .out1(demultiplexer_6_out1), .out2(demultiplexer_6_out2),
    .out3(demultiplexer_6_out3), .out4(demultiplexer_6_out4), .out5(demultiplexer_6_out5),
    .out6(demultiplexer_6_out6), .out7(demultiplexer_6_out7), .in(rom_1_data_2), .sel(rom_1_data_3));  // open: out8, out9, out10, out11, out12, out13, out14, out15
  and JNZ (JNZ_out, rom_1_data_3[15], not_20_out, rom_1_data_3[13], not_21_out);
  and JN (JN_out, rom_1_data_3[15], not_22_out, rom_1_data_3[13], rom_1_data_3[12]);
  not not_20 (not_20_out, rom_1_data_3[14]);
  not not_21 (not_21_out, rom_1_data_3[12]);
  not not_22 (not_22_out, rom_1_data_3[14]);
  Multiplexer #(.select(4), .width(3)) multiplexer_6 (
    .in0(demultiplexer_6_out0), .in1(demultiplexer_6_out1), .in2(3'b000), .in3(demultiplexer_6_out3),
    .in4(demultiplexer_6_out4), .in5(demultiplexer_6_out5), .in6(demultiplexer_6_out6), .in7(3'b000),
    .in8(3'b000), .in9(3'b000), .in10(3'b000), .in11(3'b000), .in12(3'b000), .in13(3'b000), .in14(3'b000),
    .in15(3'b000), .out(multiplexer_6_out), .sel(rom_1_data_3));
  Multiplexer #(.select(4), .width(16)) multiplexer_7 (
    .in0(demultiplexer_9_out0), .in1(multiplexer_11_out), .in2({16{1'b0}}), .in3(adder_1_out),
    .in4(subtractor_1_out), .in5(and_24_out), .in6(or_12_out), .in7({16{1'b0}}), .in8({16{1'b0}}),
    .in9({16{1'b0}}), .in10({16{1'b0}}), .in11({16{1'b0}}), .in12({16{1'b0}}), .in13({16{1'b0}}),
    .in14({16{1'b0}}), .in15({16{1'b0}}), .out(multiplexer_7_out), .sel(rom_1_data_3));
  Multiplexer #(.select(4), .width(3)) multiplexer_8 (
    .in0(demultiplexer_6_out0), .in1(demultiplexer_6_out1), .in2(3'b000), .in3(demultiplexer_6_out3),
    .in4(demultiplexer_6_out4), .in5(demultiplexer_6_out5), .in6(demultiplexer_6_out6), .in7(3'b000),
    .in8(3'b000), .in9(3'b000), .in10(3'b000), .in11(3'b000), .in12(3'b000), .in13(3'b000), .in14(3'b000),
    .in15(3'b000), .out(multiplexer_8_out), .sel(rom_1_data_3));
  Multiplexer #(.select(4), .width(16)) multiplexer_9 (
    .in0({16{1'b0}}), .in1({16{1'b0}}), .in2(demultiplexer_8_out1), .in3({16{1'b0}}), .in4({16{1'b0}}),
    .in5({16{1'b0}}), .in6({16{1'b0}}), .in7({16{1'b0}}), .in8({16{1'b0}}), .in9({16{1'b0}}),
    .in10({16{1'b0}}), .in11({16{1'b0}}), .in12({16{1'b0}}), .in13({16{1'b0}}), .in14({16{1'b0}}),
    .in15({16{1'b0}}), .out(multiplexer_9_out), .sel(rom_1_data_3));
  Multiplexer #(.select(4), .width(4)) multiplexer_10 (
    .in0(4'b0000), .in1(4'b0000), .in2(priority_encoder_1_out), .in3(4'b0000), .in4(4'b0000), .in5(4'b0000),
    .in6(4'b0000), .in7(4'b0000), .in8(4'b0000), .in9(4'b0000), .in10(4'b0000), .in11(4'b0000),
    .in12(4'b0000), .in13(4'b0000), .in14(4'b0000), .in15(4'b0000), .out(multiplexer_10_out),
    .sel(rom_1_data_3));
  Multiplexer #(.width(16)) multiplexer_11 (
    .in0(ram_1_dout), .in1(demultiplexer_3_out1), .out(multiplexer_11_out), .sel(comparator_1_gt));
  Register #(.width(16)) R4 (
    .D(demultiplexer_1_out4), .en(decoder_2_out4), .clk(clock_1_out), .Q(R4_q), .clr(CPU_Reset));
  Demultiplexer #(.select(4), .width(3)) demultiplexer_7 (
    .out0(demultiplexer_7_out0), .out3(demultiplexer_7_out3), .out4(demultiplexer_7_out4),
    .out5(demultiplexer_7_out5), .out6(demultiplexer_7_out6), .out7(demultiplexer_7_out7), .in(rom_1_data),
    .sel(rom_1_data_3));  // open: out1, out2, out8, out9, out10, out11, out12, out13, out14, out15
  Demultiplexer #(.width(16)) demultiplexer_8 (
    .out0(demultiplexer_8_out0), .out1(demultiplexer_8_out1), .in(demultiplexer_5_out2), .sel(comparator_2_gt));
  not not_23 (not_23_out, rom_1_data_3[15]);
  not not_24 (not_24_out, and_1_out);
  not not_25 (not_25_out, rom_1_data_3[13]);
  or or_4 (or_4_out, rom_1_data_3[14], not_25_out, rom_1_data_3[12]);
  and and_9 (and_9_out, not_23_out, or_4_out);
  D_Flip_Flop d_ff_3 (.D(and_9_out), .clk(clock_1_out), .Q(d_ff_3_q), .reset(not_24_out));  // open: Qn, preset
  not not_26 (not_26_out, rom_1_data_3[15]);
  not not_27 (not_27_out, rom_1_data_3[14]);
  and and_10 (and_10_out, not_26_out, not_27_out);
  Multiplexer multiplexer_12 (.in0(and_9_out), .in1(d_ff_3_q), .out(multiplexer_12_out), .sel(and_1_out));
  and and_11 (and_11_out, and_10_out, xor_1_out);
  Register #(.width(16)) R3 (
    .D(demultiplexer_1_out3), .en(decoder_2_out3), .clk(clock_1_out), .Q(R3_q), .clr(CPU_Reset));
  xor xor_1 (xor_1_out, rom_1_data_3[13], rom_1_data_3[12]);
  and and_12 (and_12_out, and_11_out, comparator_2_gt);
  Comparator #(.width(16)) comparator_1 (.a(demultiplexer_9_out1), .b(16'h33), .gt(comparator_1_gt));  // open: eq, lt
  Comparator #(.width(16)) comparator_2 (.a(demultiplexer_9_out2), .b(16'h33), .gt(comparator_2_gt));  // open: eq, lt
  Multiplexer #(.width(16)) multiplexer_13 (
    .in0(or_6_out), .in1({16{1'b0}}), .out({multiplexer_13_out_2, multiplexer_13_out}), .sel(or_5_out));
  or or_5 (or_5_out, comparator_2_gt, comparator_1_gt);
  Demultiplexer #(.select(4), .width(16)) demultiplexer_9 (
    .out0(demultiplexer_9_out0), .out1(demultiplexer_9_out1), .out2(demultiplexer_9_out2),
    .in({{7{1'b0}}, demultiplexer_7_out0, rom_1_data_4}), .sel(rom_1_data_3));  // open: out3, out4, out5, out6, out7, out8, out9, out10, out11, out12, out13, out14, out15
  not not_28 (not_28_out, rom_1_data_4[3]);
  not not_29 (not_29_out, rom_1_data_4[1]);
  and BT_Reg_Addr (BT_Reg_Addr_out, rom_1_data_4[5], rom_1_data_4[4], not_28_out, rom_1_data_4[2], not_29_out, not_30_out);
  assign or_6_out = demultiplexer_9_out2 | demultiplexer_9_out1;  // OR_Gate or_6, 16 bits wide
  Register #(.width(16)) R2 (
    .D(demultiplexer_1_out2), .en(decoder_2_out2), .clk(clock_1_out), .Q(R2_q), .clr(CPU_Reset));
  not not_30 (not_30_out, rom_1_data_4[0]);
  not not_31 (not_31_out, rom_1_data_4[3]);
  not not_32 (not_32_out, rom_1_data_4[1]);
  and SW_Reg_Addr (SW_Reg_Addr_out, rom_1_data_4[5], rom_1_data_4[4], not_31_out, rom_1_data_4[2], not_32_out, rom_1_data_4[0]);
  not not_33 (not_33_out, rom_1_data_4[3]);
  and LED_Reg_Addr (LED_Reg_Addr_out, rom_1_data_4[5], rom_1_data_4[4], not_33_out, rom_1_data_4[2], rom_1_data_4[1], not_34_out);
  not not_34 (not_34_out, rom_1_data_4[0]);
  not not_35 (not_35_out, rom_1_data_4[3]);
  and RGB_Reg_Addr (RGB_Reg_Addr_out, rom_1_data_4[5], rom_1_data_4[4], not_35_out, rom_1_data_4[2], rom_1_data_4[1], rom_1_data_4[0]);
  not not_36 (not_36_out, rom_1_data_4[0]);
  not not_37 (not_37_out, rom_1_data_4[1]);
  not not_38 (not_38_out, rom_1_data_4[2]);
  and Seg_7_Addr (Seg_7_Addr_out, rom_1_data_4[5], rom_1_data_4[4], rom_1_data_4[3], not_38_out, not_37_out, not_36_out);
  Register #(.width(16)) R1 (
    .D(demultiplexer_1_out1), .en(decoder_2_out1), .clk(clock_1_out), .Q(R1_q), .clr(CPU_Reset));
  not not_39 (not_39_out, rom_1_data_4[1]);
  not not_40 (not_40_out, rom_1_data_4[2]);
  and Seg_6_Addr (Seg_6_Addr_out, rom_1_data_4[5], rom_1_data_4[4], rom_1_data_4[3], not_40_out, not_39_out, rom_1_data_4[0]);
  not not_41 (not_41_out, rom_1_data_4[0]);
  not not_42 (not_42_out, rom_1_data_4[2]);
  and Seg_5_Addr (Seg_5_Addr_out, rom_1_data_4[5], rom_1_data_4[4], rom_1_data_4[3], not_42_out, rom_1_data_4[1], not_41_out);
  not not_43 (not_43_out, rom_1_data_4[2]);
  and Seg_4_Addr (Seg_4_Addr_out, rom_1_data_4[5], rom_1_data_4[4], rom_1_data_4[3], not_43_out, rom_1_data_4[1], rom_1_data_4[0]);
  not not_44 (not_44_out, rom_1_data_4[1]);
  and Seg_3_Addr (Seg_3_Addr_out, rom_1_data_4[5], rom_1_data_4[4], rom_1_data_4[3], rom_1_data_4[2], not_44_out, not_45_out);
  Button Left (.out(Right_out[2]));
  not not_45 (not_45_out, rom_1_data_4[0]);
  not not_46 (not_46_out, rom_1_data_4[1]);
  and Seg_2_Addr (Seg_2_Addr_out, rom_1_data_4[5], rom_1_data_4[4], rom_1_data_4[3], rom_1_data_4[2], not_46_out, rom_1_data_4[0]);
  Button Up (.out(Right_out[3]));
  Button Enter (.out(Right_out[4]));
  Button Down (.out(Right_out[1]));
  and Seg_1_Addr (Seg_1_Addr_out, rom_1_data_4[5], rom_1_data_4[4], rom_1_data_4[3], rom_1_data_4[2], rom_1_data_4[1], not_47_out);
  Register #(.width(16)) R0 (
    .D(demultiplexer_1_out0), .en(decoder_2_out0), .clk(clock_1_out), .Q(R0_q), .clr(CPU_Reset));
  // DipSwitch #(.number(16)) dipswitch_1: pin names not known
  Button Right (.out(Right_out[0]));
  not not_47 (not_47_out, rom_1_data_4[0]);
  and Seg_0_Addr (Seg_0_Addr_out, rom_1_data_4[5], rom_1_data_4[4], rom_1_data_4[3], rom_1_data_4[2], rom_1_data_4[1], rom_1_data_4[0]);
  or or_7 (or_7_out, LED_Reg_Addr_out, RGB_Reg_Addr_out, Seg_7_Addr_out, Seg_6_Addr_out, Seg_5_Addr_out, Seg_4_Addr_out, Seg_3_Addr_out, Seg_2_Addr_out, Seg_1_Addr_out, Seg_0_Addr_out);
  Priority_Encoder #(.select(4)) priority_encoder_1 (
    .in0(Seg_0_Addr_out), .in1(Seg_1_Addr_out), .in2(Seg_2_Addr_out), .in3(Seg_3_Addr_out),
    .in4(Seg_4_Addr_out), .in5(Seg_5_Addr_out), .in6(Seg_6_Addr_out), .in7(Seg_7_Addr_out),
    .in8(RGB_Reg_Addr_out), .in9(LED_Reg_Addr_out), .in10(1'b0), .in11(1'b0), .in12(1'b0), .in13(1'b0),
    .in14(1'b0), .in15(1'b0), .out(priority_encoder_1_out), .en_in(or_7_out));  // open: gs, en_out
  Priority_Encoder #(.select(1)) priority_encoder_2 (
    .in0(SW_Reg_Addr_out), .in1(BT_Reg_Addr_out), .out(priority_encoder_2_out), .en_in(BT_Reg_Addr_out));  // open: gs, en_out
  Register #(.width(16)) BT_Reg (
    .D({{11{1'b0}}, Right_out}), .en(1'b1), .clk(clock_1_out), .Q(BT_Reg_q), .clr(CPU_Reset));
  // Priority_Encoder priority_encoder_3: pin names not known; wires that end beside it: priority_encoder_3_p1, priority_encoder_3_p2, priority_encoder_3_p3, priority_encoder_3_p4, priority_encoder_3_p5, priority_encoder_3_p6, priority_encoder_3_p7, 1'b0, 1'b0, 1'b0
  not not_48 (not_48_out, rom_1_data_3[15]);
  not not_49 (not_49_out, rom_1_data_3[14]);
  and and_13 (priority_encoder_3_p3, not_48_out, not_49_out, rom_1_data_3[13], rom_1_data_3[12]);
  Register #(.width(16)) SW_Reg (.D(undriven), .en(1'b1), .clk(clock_1_out), .Q(SW_Reg_q), .clr(CPU_Reset));
  not not_50 (not_50_out, rom_1_data_3[15]);
  or or_8 (priority_encoder_3_p2, priority_encoder_3_p3, priority_encoder_3_p4, priority_encoder_3_p5, priority_encoder_3_p6, priority_encoder_3_p7);
  _7_Segment_Display u_7_segment_display_1 (
    .g(multiplexer_23_out[6]), .f(multiplexer_23_out[5]), .a(multiplexer_23_out[0]),
    .b(multiplexer_23_out[1]), .e(multiplexer_23_out[4]), .d(multiplexer_23_out[3]), .c(multiplexer_23_out[2]));  // open: dp
  not not_51 (not_51_out, rom_1_data_3[13]);
  not not_52 (not_52_out, rom_1_data_3[15]);
  not not_53 (not_53_out, rom_1_data_3[12]);
  and and_14 (priority_encoder_3_p4, not_50_out, rom_1_data_3[14], not_51_out, not_53_out);
  Register #(.width(16)) LED_Reg (
    .D(demultiplexer_2_out9), .en(decoder_1_out9), .clk(clock_1_out), .Q(LED_Reg_q), .clr(CPU_Reset));
  // RGBLED RGB: pin names not known; wires that end beside it: RGB_p2[2], RGB_p2[0], RGB_p2[1]
  _7_Segment_Display u_7_segment_display_2 (
    .g(multiplexer_21_out[6]), .f(multiplexer_21_out[5]), .a(multiplexer_21_out[0]),
    .b(multiplexer_21_out[1]), .e(multiplexer_21_out[4]), .d(multiplexer_21_out[3]), .c(multiplexer_21_out[2]));  // open: dp
  _7_Segment_Display u_7_segment_display_3 (
    .g(multiplexer_19_out[6]), .f(multiplexer_19_out[5]), .a(multiplexer_19_out[0]),
    .b(multiplexer_19_out[1]), .e(multiplexer_19_out[4]), .d(multiplexer_19_out[3]), .c(multiplexer_19_out[2]));  // open: dp
  not not_54 (not_54_out, rom_1_data_3[13]);
  and and_15 (priority_encoder_3_p5, not_52_out, rom_1_data_3[14], not_54_out, rom_1_data_3[12]);
  // LedBar #(.inputtype("row"), .matrixcols(16)) ledbar_1: pin names not known; wires that end beside it: LED_Reg_q
  _7_Segment_Display u_7_segment_display_4 (
    .g(multiplexer_17_out[6]), .f(multiplexer_17_out[5]), .a(multiplexer_17_out[0]),
    .b(multiplexer_17_out[1]), .e(multiplexer_17_out[4]), .d(multiplexer_17_out[3]), .c(multiplexer_17_out[2]));  // open: dp
  _7_Segment_Display u_7_segment_display_5 (
    .g(multiplexer_22_out[6]), .f(multiplexer_22_out[5]), .a(multiplexer_22_out[0]),
    .b(multiplexer_22_out[1]), .e(multiplexer_22_out[4]), .d(multiplexer_22_out[3]), .c(multiplexer_22_out[2]));  // open: dp
  not not_55 (not_55_out, rom_1_data_3[15]);
  not not_56 (not_56_out, rom_1_data_3[12]);
  and and_16 (priority_encoder_3_p6, not_55_out, rom_1_data_3[14], rom_1_data_3[13], not_56_out);
  Register #(.width(16)) RGB_Reg (
    .D(demultiplexer_2_out8), .en(decoder_1_out8), .clk(clock_1_out), .Q(RGB_p2), .clr(CPU_Reset));
  _7_Segment_Display u_7_segment_display_6 (
    .g(multiplexer_20_out[6]), .f(multiplexer_20_out[5]), .a(multiplexer_20_out[0]),
    .b(multiplexer_20_out[1]), .e(multiplexer_20_out[4]), .d(multiplexer_20_out[3]), .c(multiplexer_20_out[2]));  // open: dp
  not not_57 (not_57_out, rom_1_data_3[15]);
  and and_17 (priority_encoder_3_p7, not_57_out, rom_1_data_3[14], rom_1_data_3[13], rom_1_data_3[12]);
  Register #(.width(16)) Seg7 (
    .D(demultiplexer_2_out7), .en(decoder_1_out7), .clk(clock_1_out), .Q(Seg7_q), .clr(CPU_Reset));
  _7_Segment_Display u_7_segment_display_7 (
    .g(multiplexer_18_out[6]), .f(multiplexer_18_out[5]), .a(multiplexer_18_out[0]),
    .b(multiplexer_18_out[1]), .e(multiplexer_18_out[4]), .d(multiplexer_18_out[3]), .c(multiplexer_18_out[2]));  // open: dp
  // DipSwitch #(.number(16)) dipswitch_2: pin names not known
  _7_Segment_Display u_7_segment_display_8 (
    .g(multiplexer_16_out[6]), .f(multiplexer_16_out[5]), .a(multiplexer_16_out[0]),
    .b(multiplexer_16_out[1]), .e(multiplexer_16_out[4]), .d(multiplexer_16_out[3]), .c(multiplexer_16_out[2]));  // open: dp
  Register #(.width(16)) Seg6 (
    .D(demultiplexer_2_out6), .en(decoder_1_out6), .clk(clock_1_out), .Q(Seg6_q), .clr(CPU_Reset));
  Register #(.width(16)) Seg5 (
    .D(demultiplexer_2_out5), .en(decoder_1_out5), .clk(clock_1_out), .Q(Seg5_q), .clr(CPU_Reset));
  Register #(.width(16)) Seg4 (
    .D(demultiplexer_2_out4), .en(decoder_1_out4), .clk(clock_1_out), .Q(Seg4_q), .clr(CPU_Reset));
  Register #(.width(16)) Seg3 (
    .D(demultiplexer_2_out3), .en(decoder_1_out3), .clk(clock_1_out), .Q(Seg3_q), .clr(CPU_Reset));
  Register #(.width(16)) Seg2 (
    .D(demultiplexer_2_out2), .en(decoder_1_out2), .clk(clock_1_out), .Q(Seg2_q), .clr(CPU_Reset));
  Register #(.width(16)) Seg1 (
    .D(demultiplexer_2_out1), .en(decoder_1_out1), .clk(clock_1_out), .Q(Seg1_q), .clr(CPU_Reset));
  not not_58 (not_58_out, Seg0_q[7]);
  not not_59 (not_59_out, Seg0_q[2]);
  Register #(.width(16)) Seg0 (
    .D(demultiplexer_2_out0), .en(decoder_1_out0), .clk(clock_1_out),
    .Q({Seg0_q[15:4], Seg0_q[7], Seg0_q[2:0]}), .clr(CPU_Reset));
  not not_60 (not_60_out, Seg0_q[0]);
  not not_61 (not_61_out, Seg0_q[7]);
  and and_18 (and_18_out, not_58_out, not_59_out, Seg0_q[1], not_60_out);
  or or_9 (or_9_out, and_18_out, priority_encoder_4_p4);
  // Priority_Encoder #(.select(2)) priority_encoder_4: pin names not known; wires that end beside it: 1'b0, and_18_out, priority_encoder_4_p3, priority_encoder_4_p4, 1'b0, or_9_out, priority_encoder_4_p3
  not not_62 (not_62_out, Seg0_q[1]);
  not not_63 (not_63_out, Seg0_q[0]);
  and and_19 (priority_encoder_4_p4, not_61_out, Seg0_q[2], not_62_out, not_63_out);
  Multiplexer #(.select(2), .width(4)) multiplexer_14 (
    .in0({Seg0_q[7], Seg0_q[2:0]}), .in1(4'b0001), .in2(4'b0010), .out(multiplexer_14_out));  // open: in3, sel
  not not_64 (not_64_out, multiplexer_14_out[0]);
  not not_65 (not_65_out, multiplexer_14_out[1]);
  not not_66 (not_66_out, multiplexer_14_out[2]);
  not not_67 (not_67_out, multiplexer_14_out[3]);
  not not_68 (not_68_out, Seg0_q[4]);
  not not_69 (not_69_out, Seg0_q[5]);
  not not_70 (not_70_out, Seg0_q[7]);
  not not_71 (not_71_out, multiplexer_14_out[0]);
  not not_72 (not_72_out, multiplexer_14_out[1]);
  not not_73 (not_73_out, multiplexer_14_out[2]);
  not not_74 (not_74_out, multiplexer_14_out[3]);
  not not_75 (not_75_out, Seg0_q[4]);
  not not_76 (not_76_out, Seg0_q[5]);
  not not_77 (not_77_out, Seg0_q[6]);
  not not_78 (not_78_out, Seg4_q[0]);
  not not_79 (not_79_out, Seg4_q[1]);
  not not_80 (not_80_out, Seg4_q[2]);
  not not_81 (not_81_out, Seg4_q[3]);
  not not_82 (not_82_out, Seg4_q[4]);
  not not_83 (not_83_out, Seg4_q[5]);
  not not_84 (not_84_out, Seg4_q[7]);
  not not_85 (not_85_out, Seg4_q[0]);
  not not_86 (not_86_out, Seg4_q[1]);
  not not_87 (not_87_out, Seg4_q[2]);
  not not_88 (not_88_out, Seg4_q[3]);
  not not_89 (not_89_out, Seg4_q[4]);
  not not_90 (not_90_out, Seg4_q[5]);
  not not_91 (not_91_out, Seg4_q[6]);
  not not_92 (not_92_out, Seg4_q[2]);
  not not_93 (not_93_out, Seg4_q[3]);
  not not_94 (not_94_out, Seg4_q[7]);
  not not_95 (not_95_out, Seg4_q[1]);
  not not_96 (not_96_out, Seg4_q[2]);
  not not_97 (not_97_out, Seg4_q[3]);
  not not_98 (not_98_out, Seg4_q[7]);
  not not_99 (not_99_out, Seg4_q[0]);
  not not_100 (not_100_out, Seg4_q[1]);
  not not_101 (not_101_out, Seg4_q[2]);
  not not_102 (not_102_out, Seg4_q[3]);
  not not_103 (not_103_out, Seg4_q[6]);
  not not_104 (not_104_out, Seg4_q[7]);
  not not_105 (not_105_out, Seg4_q[0]);
  not not_106 (not_106_out, Seg4_q[1]);
  not not_107 (not_107_out, Seg4_q[2]);
  not not_108 (not_108_out, Seg4_q[6]);
  not not_109 (not_109_out, Seg4_q[7]);
  and and_20 (and_20_out, not_64_out, not_65_out, not_66_out, not_67_out, not_68_out, not_69_out, Seg0_q[6], not_70_out);
  and and_21 (and_21_out, not_71_out, not_72_out, not_73_out, not_74_out, not_75_out, not_76_out, not_77_out, Seg0_q[7]);
  and and_22 (and_22_out, not_78_out, not_79_out, not_80_out, not_81_out, not_82_out, not_83_out, Seg4_q[6], not_84_out);
  and and_23 (and_23_out, not_85_out, not_86_out, not_87_out, not_88_out, not_89_out, not_90_out, not_91_out, Seg4_q[7]);
  and P_Seg4 (P_Seg4_out, Seg4_q[0], Seg4_q[1], not_92_out, not_93_out, Seg4_q[4], Seg4_q[5], Seg4_q[6], not_94_out);
  and F_Seg4 (F_Seg4_out, Seg4_q[0], not_95_out, not_96_out, not_97_out, Seg4_q[4], Seg4_q[5], Seg4_q[6], not_98_out);
  and I_Seg4 (I_Seg4_out, not_99_out, not_100_out, not_101_out, not_102_out, Seg4_q[4], Seg4_q[5], not_103_out, not_104_out);
  and L_Seg4 (L_Seg4_out, not_105_out, not_106_out, not_107_out, Seg4_q[3], Seg4_q[4], Seg4_q[5], not_108_out, not_109_out);
  BCH_7seg Seg0_Decoder (
    .A(multiplexer_14_out[3]), .B(multiplexer_14_out[2]), .C(multiplexer_14_out[1]),
    .D(multiplexer_14_out[0]), .a_2(Seg0_Decoder_a_2[0]), .b_2(Seg0_Decoder_a_2[1]),
    .c_2(Seg0_Decoder_a_2[2]), .d_2(Seg0_Decoder_a_2[3]), .e(Seg0_Decoder_a_2[4]), .f(Seg0_Decoder_a_2[5]),
    .g(Seg0_Decoder_a_2[6]));
  BCH_7seg Seg4_Decoder (
    .A(Seg4_q[3]), .B(Seg4_q[2]), .C(Seg4_q[1]), .D(Seg4_q[0]), .a_2(Seg4_Decoder_a_2[0]),
    .b_2(Seg4_Decoder_a_2[1]), .c_2(Seg4_Decoder_a_2[2]), .d_2(Seg4_Decoder_a_2[3]), .e(Seg4_Decoder_a_2[4]),
    .f(Seg4_Decoder_a_2[5]), .g(Seg4_Decoder_a_2[6]));
  or or_10 (or_10_out, and_20_out, and_21_out);
  or or_11 (or_11_out, and_22_out, and_23_out, P_Seg4_out, F_Seg4_out, I_Seg4_out, L_Seg4_out);
  Multiplexer #(.select(3), .width(16)) multiplexer_15 (
    .in0(adder_1_out), .in1(subtractor_1_out), .in2(and_24_out), .in3(or_12_out), .in4(demultiplexer_5_out7),
    .out(multiplexer_15_out));  // open: in5, in6, in7, sel
  Multiplexer #(.width(16)) multiplexer_16 (
    .in0(Seg0_Decoder_a_2), .in1({Seg0_q[15:4], Seg0_q[7], Seg0_q[2:0]}), .out(multiplexer_16_out),
    .sel(or_10_out));
  Multiplexer #(.width(16)) multiplexer_17 (
    .in0(Seg4_Decoder_a_2), .in1(Seg4_q), .out(multiplexer_17_out), .sel(or_11_out));
  Adder #(.width(16)) adder_1 (
    .a(demultiplexer_5_out3), .b(demultiplexer_4_out3), .out(adder_1_out));  // open: cin, cout
  Subtractor #(.width(16)) subtractor_1 (
    .a(demultiplexer_5_out4), .b(demultiplexer_4_out4), .out(subtractor_1_out));  // open: bin, bout
  assign and_24_out = demultiplexer_5_out5 & demultiplexer_4_out5;  // AND_Gate and_24, 16 bits wide
  assign or_12_out = demultiplexer_5_out6 | demultiplexer_4_out6;  // OR_Gate or_12, 16 bits wide
  Comparator #(.width(16)) comparator_3 (
    .a(multiplexer_15_out), .b(demultiplexer_4_out7), .eq(comparator_3_eq), .lt(comparator_3_lt));  // open: gt
  not not_110 (not_110_out, Seg1_q[0]);
  not not_111 (not_111_out, Seg1_q[1]);
  not not_112 (not_112_out, Seg1_q[2]);
  not not_113 (not_113_out, Seg1_q[3]);
  not not_114 (not_114_out, Seg1_q[4]);
  not not_115 (not_115_out, Seg1_q[5]);
  not not_116 (not_116_out, Seg1_q[7]);
  not not_117 (not_117_out, Seg1_q[0]);
  not not_118 (not_118_out, Seg1_q[1]);
  not not_119 (not_119_out, Seg1_q[2]);
  not not_120 (not_120_out, Seg1_q[3]);
  not not_121 (not_121_out, Seg1_q[4]);
  not not_122 (not_122_out, Seg1_q[5]);
  not not_123 (not_123_out, Seg1_q[6]);
  not not_124 (not_124_out, Seg5_q[0]);
  not not_125 (not_125_out, Seg5_q[1]);
  not not_126 (not_126_out, Seg5_q[2]);
  not not_127 (not_127_out, Seg5_q[3]);
  not not_128 (not_128_out, Seg5_q[4]);
  not not_129 (not_129_out, Seg5_q[5]);
  not not_130 (not_130_out, Seg5_q[7]);
  not not_131 (not_131_out, Seg5_q[0]);
  not not_132 (not_132_out, Seg5_q[1]);
  not not_133 (not_133_out, Seg5_q[2]);
  not not_134 (not_134_out, Seg5_q[3]);
  not not_135 (not_135_out, Seg5_q[4]);
  not not_136 (not_136_out, Seg5_q[5]);
  not not_137 (not_137_out, Seg5_q[6]);
  not not_138 (not_138_out, Seg5_q[2]);
  not not_139 (not_139_out, Seg5_q[3]);
  not not_140 (not_140_out, Seg5_q[7]);
  not not_141 (not_141_out, Seg5_q[1]);
  not not_142 (not_142_out, Seg5_q[2]);
  not not_143 (not_143_out, Seg5_q[3]);
  not not_144 (not_144_out, Seg5_q[7]);
  not not_145 (not_145_out, Seg5_q[0]);
  not not_146 (not_146_out, Seg5_q[1]);
  not not_147 (not_147_out, Seg5_q[2]);
  not not_148 (not_148_out, Seg5_q[3]);
  not not_149 (not_149_out, Seg5_q[6]);
  not not_150 (not_150_out, Seg5_q[7]);
  not not_151 (not_151_out, Seg5_q[0]);
  not not_152 (not_152_out, Seg5_q[1]);
  not not_153 (not_153_out, Seg5_q[2]);
  not not_154 (not_154_out, Seg5_q[6]);
  not not_155 (not_155_out, Seg5_q[7]);
  and and_25 (and_25_out, not_110_out, not_111_out, not_112_out, not_113_out, not_114_out, not_115_out, Seg1_q[6], not_116_out);
  and and_26 (and_26_out, not_117_out, not_118_out, not_119_out, not_120_out, not_121_out, not_122_out, not_123_out, Seg1_q[7]);
  and and_27 (and_27_out, not_124_out, not_125_out, not_126_out, not_127_out, not_128_out, not_129_out, Seg5_q[6], not_130_out);
  and and_28 (and_28_out, not_131_out, not_132_out, not_133_out, not_134_out, not_135_out, not_136_out, not_137_out, Seg5_q[7]);
  and and_29 (and_29_out, Seg5_q[0], Seg5_q[1], not_138_out, not_139_out, Seg5_q[4], Seg5_q[5], Seg5_q[6], not_140_out);
  and and_30 (and_30_out, Seg5_q[0], not_141_out, not_142_out, not_143_out, Seg5_q[4], Seg5_q[5], Seg5_q[6], not_144_out);
  and and_31 (and_31_out, not_145_out, not_146_out, not_147_out, not_148_out, Seg5_q[4], Seg5_q[5], not_149_out, not_150_out);
  and and_32 (and_32_out, not_151_out, not_152_out, not_153_out, Seg5_q[3], Seg5_q[4], Seg5_q[5], not_154_out, not_155_out);
  BCH_7seg Seg1_Decoder (
    .A(Seg1_q[3]), .B(Seg1_q[2]), .C(Seg1_q[1]), .D(Seg1_q[0]), .a_2(Seg1_Decoder_a_2[0]),
    .b_2(Seg1_Decoder_a_2[1]), .c_2(Seg1_Decoder_a_2[2]), .d_2(Seg1_Decoder_a_2[3]), .e(Seg1_Decoder_a_2[4]),
    .f(Seg1_Decoder_a_2[5]), .g(Seg1_Decoder_a_2[6]));
  BCH_7seg Seg5_Decoder (
    .A(Seg5_q[3]), .B(Seg5_q[2]), .C(Seg5_q[1]), .D(Seg5_q[0]), .a_2(Seg5_Decoder_a_2[0]),
    .b_2(Seg5_Decoder_a_2[1]), .c_2(Seg5_Decoder_a_2[2]), .d_2(Seg5_Decoder_a_2[3]), .e(Seg5_Decoder_a_2[4]),
    .f(Seg5_Decoder_a_2[5]), .g(Seg5_Decoder_a_2[6]));
  or or_13 (or_13_out, and_25_out, and_26_out);
  or or_14 (or_14_out, and_27_out, and_28_out, and_29_out, and_30_out, and_31_out, and_32_out);
  D_Flip_Flop Z_flag_reg (.D(comparator_3_eq), .clk(clock_1_out), .Q(Z_flag_reg_q));  // open: Qn, preset, reset
  D_Flip_Flop N_flag_reg (.D(comparator_3_lt), .clk(clock_1_out), .Q(N_flag_reg_q));  // open: Qn, preset, reset
  Multiplexer #(.width(16)) multiplexer_18 (
    .in0(Seg1_Decoder_a_2), .in1(Seg1_q), .out(multiplexer_18_out), .sel(or_13_out));
  Multiplexer #(.width(16)) multiplexer_19 (
    .in0(Seg5_Decoder_a_2), .in1(Seg5_q), .out(multiplexer_19_out), .sel(or_14_out));
  not not_156 (not_156_out, Seg2_q[0]);
  not not_157 (not_157_out, Seg2_q[1]);
  not not_158 (not_158_out, Seg2_q[2]);
  not not_159 (not_159_out, Seg2_q[3]);
  not not_160 (not_160_out, Seg2_q[4]);
  not not_161 (not_161_out, Seg2_q[5]);
  not not_162 (not_162_out, Seg2_q[7]);
  not not_163 (not_163_out, Seg2_q[0]);
  not not_164 (not_164_out, Seg2_q[1]);
  not not_165 (not_165_out, Seg2_q[2]);
  not not_166 (not_166_out, Seg2_q[3]);
  not not_167 (not_167_out, Seg2_q[4]);
  not not_168 (not_168_out, Seg2_q[5]);
  not not_169 (not_169_out, Seg2_q[6]);
  not not_170 (not_170_out, Seg6_q[0]);
  not not_171 (not_171_out, Seg6_q[1]);
  not not_172 (not_172_out, Seg6_q[2]);
  not not_173 (not_173_out, Seg6_q[3]);
  not not_174 (not_174_out, Seg6_q[4]);
  not not_175 (not_175_out, Seg6_q[5]);
  not not_176 (not_176_out, Seg6_q[7]);
  not not_177 (not_177_out, Seg6_q[0]);
  not not_178 (not_178_out, Seg6_q[1]);
  not not_179 (not_179_out, Seg6_q[2]);
  not not_180 (not_180_out, Seg6_q[3]);
  not not_181 (not_181_out, Seg6_q[4]);
  not not_182 (not_182_out, Seg6_q[5]);
  not not_183 (not_183_out, Seg6_q[6]);
  not not_184 (not_184_out, Seg6_q[2]);
  not not_185 (not_185_out, Seg6_q[3]);
  not not_186 (not_186_out, Seg6_q[7]);
  not not_187 (not_187_out, Seg6_q[1]);
  not not_188 (not_188_out, Seg6_q[2]);
  not not_189 (not_189_out, Seg6_q[3]);
  not not_190 (not_190_out, Seg6_q[7]);
  not not_191 (not_191_out, Seg6_q[0]);
  not not_192 (not_192_out, Seg6_q[1]);
  not not_193 (not_193_out, Seg6_q[2]);
  not not_194 (not_194_out, Seg6_q[3]);
  not not_195 (not_195_out, Seg6_q[6]);
  not not_196 (not_196_out, Seg6_q[7]);
  not not_197 (not_197_out, Seg6_q[0]);
  not not_198 (not_198_out, Seg6_q[1]);
  not not_199 (not_199_out, Seg6_q[2]);
  not not_200 (not_200_out, Seg6_q[6]);
  not not_201 (not_201_out, Seg6_q[7]);
  and and_33 (and_33_out, not_156_out, not_157_out, not_158_out, not_159_out, not_160_out, not_161_out, Seg2_q[6], not_162_out);
  and and_34 (and_34_out, not_163_out, not_164_out, not_165_out, not_166_out, not_167_out, not_168_out, not_169_out, Seg2_q[7]);
  and and_35 (and_35_out, not_170_out, not_171_out, not_172_out, not_173_out, not_174_out, not_175_out, Seg6_q[6], not_176_out);
  and and_36 (and_36_out, not_177_out, not_178_out, not_179_out, not_180_out, not_181_out, not_182_out, not_183_out, Seg6_q[7]);
  and and_37 (and_37_out, Seg6_q[0], Seg6_q[1], not_184_out, not_185_out, Seg6_q[4], Seg6_q[5], Seg6_q[6], not_186_out);
  and and_38 (and_38_out, Seg6_q[0], not_187_out, not_188_out, not_189_out, Seg6_q[4], Seg6_q[5], Seg6_q[6], not_190_out);
  and and_39 (and_39_out, not_191_out, not_192_out, not_193_out, not_194_out, Seg6_q[4], Seg6_q[5], not_195_out, not_196_out);
  and and_40 (and_40_out, not_197_out, not_198_out, not_199_out, Seg6_q[3], Seg6_q[4], Seg6_q[5], not_200_out, not_201_out);
  BCH_7seg Seg2_Decoder (
    .A(Seg2_q[3]), .B(Seg2_q[2]), .C(Seg2_q[1]), .D(Seg2_q[0]), .a_2(Seg2_Decoder_a_2[0]),
    .b_2(Seg2_Decoder_a_2[1]), .c_2(Seg2_Decoder_a_2[2]), .d_2(Seg2_Decoder_a_2[3]), .e(Seg2_Decoder_a_2[4]),
    .f(Seg2_Decoder_a_2[5]), .g(Seg2_Decoder_a_2[6]));
  BCH_7seg Seg6_Decoder (
    .A(Seg6_q[3]), .B(Seg6_q[2]), .C(Seg6_q[1]), .D(Seg6_q[0]), .a_2(Seg6_Decoder_a_2[0]),
    .b_2(Seg6_Decoder_a_2[1]), .c_2(Seg6_Decoder_a_2[2]), .d_2(Seg6_Decoder_a_2[3]), .e(Seg6_Decoder_a_2[4]),
    .f(Seg6_Decoder_a_2[5]), .g(Seg6_Decoder_a_2[6]));
  or or_15 (or_15_out, and_33_out, and_34_out);
  or or_16 (or_16_out, and_35_out, and_36_out, and_37_out, and_38_out, and_39_out, and_40_out);
  Multiplexer #(.width(16)) multiplexer_20 (
    .in0(Seg2_Decoder_a_2), .in1(Seg2_q), .out(multiplexer_20_out), .sel(or_15_out));
  Multiplexer #(.width(16)) multiplexer_21 (
    .in0(Seg6_Decoder_a_2), .in1(Seg6_q), .out(multiplexer_21_out), .sel(or_16_out));
  not not_202 (not_202_out, Seg3_q[0]);
  not not_203 (not_203_out, Seg3_q[1]);
  not not_204 (not_204_out, Seg3_q[2]);
  not not_205 (not_205_out, Seg3_q[3]);
  not not_206 (not_206_out, Seg3_q[4]);
  not not_207 (not_207_out, Seg3_q[5]);
  not not_208 (not_208_out, Seg3_q[7]);
  not not_209 (not_209_out, Seg3_q[0]);
  not not_210 (not_210_out, Seg3_q[1]);
  not not_211 (not_211_out, Seg3_q[2]);
  not not_212 (not_212_out, Seg3_q[3]);
  not not_213 (not_213_out, Seg3_q[4]);
  not not_214 (not_214_out, Seg3_q[5]);
  not not_215 (not_215_out, Seg3_q[6]);
  not not_216 (not_216_out, Seg7_q[0]);
  not not_217 (not_217_out, Seg7_q[1]);
  not not_218 (not_218_out, Seg7_q[2]);
  not not_219 (not_219_out, Seg7_q[3]);
  not not_220 (not_220_out, Seg7_q[4]);
  not not_221 (not_221_out, Seg7_q[5]);
  not not_222 (not_222_out, Seg7_q[7]);
  not not_223 (not_223_out, Seg7_q[0]);
  not not_224 (not_224_out, Seg7_q[1]);
  not not_225 (not_225_out, Seg7_q[2]);
  not not_226 (not_226_out, Seg7_q[3]);
  not not_227 (not_227_out, Seg7_q[4]);
  not not_228 (not_228_out, Seg7_q[5]);
  not not_229 (not_229_out, Seg7_q[6]);
  not not_230 (not_230_out, Seg7_q[2]);
  not not_231 (not_231_out, Seg7_q[3]);
  not not_232 (not_232_out, Seg7_q[7]);
  not not_233 (not_233_out, Seg7_q[1]);
  not not_234 (not_234_out, Seg7_q[2]);
  not not_235 (not_235_out, Seg7_q[3]);
  not not_236 (not_236_out, Seg7_q[7]);
  not not_237 (not_237_out, Seg7_q[0]);
  not not_238 (not_238_out, Seg7_q[1]);
  not not_239 (not_239_out, Seg7_q[2]);
  not not_240 (not_240_out, Seg7_q[3]);
  not not_241 (not_241_out, Seg7_q[6]);
  not not_242 (not_242_out, Seg7_q[7]);
  not not_243 (not_243_out, Seg7_q[0]);
  not not_244 (not_244_out, Seg7_q[1]);
  not not_245 (not_245_out, Seg7_q[2]);
  not not_246 (not_246_out, Seg7_q[6]);
  not not_247 (not_247_out, Seg7_q[7]);
  and and_41 (and_41_out, not_202_out, not_203_out, not_204_out, not_205_out, not_206_out, not_207_out, Seg3_q[6], not_208_out);
  and and_42 (and_42_out, not_209_out, not_210_out, not_211_out, not_212_out, not_213_out, not_214_out, not_215_out, Seg3_q[7]);
  and and_43 (and_43_out, not_216_out, not_217_out, not_218_out, not_219_out, not_220_out, not_221_out, Seg7_q[6], not_222_out);
  and and_44 (and_44_out, not_223_out, not_224_out, not_225_out, not_226_out, not_227_out, not_228_out, not_229_out, Seg7_q[7]);
  and and_45 (and_45_out, Seg7_q[0], Seg7_q[1], not_230_out, not_231_out, Seg7_q[4], Seg7_q[5], Seg7_q[6], not_232_out);
  and and_46 (and_46_out, Seg7_q[0], not_233_out, not_234_out, not_235_out, Seg7_q[4], Seg7_q[5], Seg7_q[6], not_236_out);
  and and_47 (and_47_out, not_237_out, not_238_out, not_239_out, not_240_out, Seg7_q[4], Seg7_q[5], not_241_out, not_242_out);
  and and_48 (and_48_out, not_243_out, not_244_out, not_245_out, Seg7_q[3], Seg7_q[4], Seg7_q[5], not_246_out, not_247_out);
  BCH_7seg Seg3_Decoder (
    .A(Seg3_q[3]), .B(Seg3_q[2]), .C(Seg3_q[1]), .D(Seg3_q[0]), .a_2(Seg3_Decoder_a_2[0]),
    .b_2(Seg3_Decoder_a_2[1]), .c_2(Seg3_Decoder_a_2[2]), .d_2(Seg3_Decoder_a_2[3]), .e(Seg3_Decoder_a_2[4]),
    .f(Seg3_Decoder_a_2[5]), .g(Seg3_Decoder_a_2[6]));
  BCH_7seg Seg7_Decoder (
    .A(Seg7_q[3]), .B(Seg7_q[2]), .C(Seg7_q[1]), .D(Seg7_q[0]), .a_2(Seg7_Decoder_a_2[0]),
    .b_2(Seg7_Decoder_a_2[1]), .c_2(Seg7_Decoder_a_2[2]), .d_2(Seg7_Decoder_a_2[3]), .e(Seg7_Decoder_a_2[4]),
    .f(Seg7_Decoder_a_2[5]), .g(Seg7_Decoder_a_2[6]));
  or or_17 (or_17_out, and_41_out, and_42_out);
  or or_18 (or_18_out, and_43_out, and_44_out, and_45_out, and_46_out, and_47_out, and_48_out);
  Multiplexer #(.width(16)) multiplexer_22 (
    .in0(Seg3_Decoder_a_2), .in1(Seg3_q), .out(multiplexer_22_out), .sel(or_17_out));
  Multiplexer #(.width(16)) multiplexer_23 (
    .in0(Seg7_Decoder_a_2), .in1(Seg7_q), .out(multiplexer_23_out), .sel(or_18_out));

  // Notes on the sheet:
  //   contents of rom_1 (hex, n*v repeats v):
  //   0 201 a80 2a0b 2001 200c 2002 2003 2004 2005 2006 2007 2008 2009 200a a80 2a38 2a39 2a3a 2a3b 2a3c
  //   2a3d 2a3e 2a3f 2037 c03 a40 2a38 2a39 2a3a 2a3b 2a3c 2a3d 2a3e 2a3f e3f 4e40 a024 a80 2a38 2a39 2a3a
  //   2a3b 2a3c 2a3d 2a3e 2a3f e3f 4e40 a030 4c40 a01b a40 2a38 2a39 2a3a 2a3b a80 2a3c 2a3d 2a3e 1a0c
  //   c000 c000 2a3f 200a 2002 2003 2004 2005 2006 2007 2008 2009 1634 410 5680 7600 a04a 1634 410 5680
  //   7600 904f 1634 410 5680 7600 a054 805a 1e0a c000 c000 805e 1806 c000 c000 7800 9067 1a02 c000 c000
  //   8068 a40 2a38 1807 c000 c000 7800 9072 1a03 c000 c000 8073 a40 2a39 1808 c000 c000 7800 907d 1a04
  //   c000 c000 807e a40 2a3a 1809 c000 c000 7800 9088 1a05 c000 c000 8089 a40 2a3b 1e0a c000 c000 400
  //   7e80 9099 401 7e80 90ad 402 7e80 90c1 403 7e80 90d5 a80 2a38 c3f 4c40 a09c 1806 c000 c000 7800 90a7
  //   1a02 c000 c000 80a8 a40 2a38 c3f 4c40 a0aa 80e9 a80 2a39 c3f 4c40 a0b0 1807 c000 c000 7800 90bb 1a03
  //   c000 c000 80bc a40 2a39 c3f 4c40 a0be 80e9 a80 2a3a c3f 4c40 a0c4 1808 c000 c000 7800 90cf 1a04 c000
  //   c000 80d0 a40 2a3a c3f 4c40 a0d2 80e9 a80 2a3b c3f 4c40 a0d8 1809 c000 c000 7800 90e3 1a05 c000 c000
  //   80e4 a40 2a3b c3f 4c40 a0e6 80e9 1634 401 5680 7600 a103 1634 402 5680 7600 a165 1634 404 5680 7600
  //   a111 1634 408 5680 7600 a11e 1634 410 5680 7600 a1a8 805a 1e0a c000 c000 403 7e80 910b 3e40 2e0a
  //   1634 401 5680 7600 a10b 805a 1e0a c000 c000 7e00 9118 4e40 2e0a 1634 404 5680 7600 a118 805a 1e0a
  //   c000 c000 400 7e80 912b 401 7e80 9138 402 7e80 9145 8152 1a02 c000 c000 40f 7a80 9133 3a40 8134 a00
  //   2a02 401 2406 815f 1a03 c000 c000 40f 7a80 9140 3a40 8141 a00 2a03 401 2407 815f 1a04 c000 c000 40f
  //   7a80 914d 3a40 814e a00 2a04 401 2408 815f 1a05 c000 c000 40f 7a80 915a 3a40 815b a00 2a05 401 2409
  //   815f 1634 408 5680 7600 a15f 805a 1e0a c000 c000 400 7e80 9172 401 7e80 917e 402 7e80 918a 8196 1a02
  //   c000 c000 7a00 9179 4a40 817a a0f 2a02 401 2406 81a2 1a03 c000 c000 7a00 9185 4a40 8186 a0f 2a03 401
  //   2407 81a2 1a04 c000 c000 7a00 9191 4a40 8192 a0f 2a04 401 2408 81a2 1a05 c000 c000 7a00 919d 4a40
  //   819e a0f 2a05 401 2409 81a2 1634 402 5680 7600 a1a2 805a 1634 410 5680 7600 a1a8 800 1a02 c000 c000
  //   401 7a80 a1c7 1a03 c000 c000 407 7a80 a1c7 1a04 c000 c000 403 7a80 a1c7 1a05 c000 c000 408 7a80 a1c7
  //   81da 7800 a1d9 801 1c01 c000 c000 3c40 2c01 1a0c c000 c000 3a40 2a0c 2a3f 406 7c80 9225 820c 820c
  //   2037 a73 2a38 a0a 2a39 a05 2a3a a05 2a3b a80 2a3c 2a3d 2a3e 2a3f c03 a02 2a37 a73 2a38 a0a 2a39 a05
  //   2a3a a05 2a3b e3f 4e40 a1f4 2037 a80 2a38 2a39 2a3a 2a3b e3f 4e40 a1fd 4c40 a1e9 a02 2a37 a73 2a38
  //   a0a 2a39 a05 2a3a a05 2a3b 8201 a01 2a37 c03 a71 2a38 a0a 2a39 a30 2a3a a38 2a3b e3f 4e40 a218 a80
  //   2a38 2a39 2a3a 2a3b e3f 4e40 a220 4c40 a20f 8034 a01 2a37 c03 aff 2a38 2a39 2a3a 2a3b 2a3c 2a3d 2a3e
  //   2a3f e3f 4e40 a232 a80 2a38 2a39 2a3a 2a3b 2a3c 2a3d 2a3e 2a3f e3f 4e40 a23e 4c40 a229 d000
endmodule

module BCH_7seg (
  input  A,
  input  B,
  input  C,
  input  D,
  output a_2,
  output b_2,
  output c_2,
  output d_2,
  output e,
  output f,
  output g
);

  wire and_1_out, and_2_out, and_3_out, and_4_out, and_5_out, and_6_out, and_7_out, and_8_out, and_9_out,
       and_10_out, and_11_out, and_12_out, and_13_out, and_14_out, and_15_out, and_16_out, and_17_out,
       and_18_out, and_19_out, and_20_out, and_21_out, and_22_out, and_23_out, and_24_out, and_25_out,
       and_26_out, and_27_out, and_28_out, and_29_out, and_30_out, and_31_out, and_32_out, and_33_out,
       not_1_out, not_2_out, not_3_out, not_4_out, or_1_out, or_2_out, or_3_out, or_4_out, or_5_out,
       or_6_out, or_7_out, or_8_out, or_9_out, or_10_out, or_11_out, or_12_out, or_13_out, or_14_out,
       or_15_out, or_16_out, or_17_out;

  not not_1 (not_1_out, A);
  not not_2 (not_2_out, B);
  not not_3 (not_3_out, C);
  not not_4 (not_4_out, D);
  and and_1 (and_1_out, not_1_out, not_2_out);
  and and_2 (and_2_out, not_3_out, D);
  and and_3 (and_3_out, not_1_out, B);
  and and_4 (and_4_out, not_3_out, not_4_out);
  and and_5 (and_5_out, A, not_2_out);
  and and_6 (and_6_out, C, D);
  and and_7 (and_7_out, A, B);
  and and_8 (and_8_out, B, C);
  and and_9 (and_9_out, A, C);
  and and_10 (and_10_out, C, not_4_out);
  and and_11 (and_11_out, not_1_out, D);
  and and_12 (and_12_out, not_2_out, not_3_out);
  and and_13 (and_13_out, not_1_out, C);
  and and_14 (and_14_out, and_1_out, and_2_out);
  and and_15 (and_15_out, and_3_out, and_4_out);
  and and_16 (and_16_out, and_5_out, and_6_out);
  and and_17 (and_17_out, and_7_out, and_2_out);
  and and_18 (and_18_out, and_3_out, and_2_out);
  and and_19 (and_19_out, and_8_out, not_4_out);
  and and_20 (and_20_out, and_9_out, D);
  and and_21 (and_21_out, and_7_out, not_4_out);
  and and_22 (and_22_out, and_1_out, and_10_out);
  and and_23 (and_23_out, and_7_out, C);
  and and_24 (and_24_out, and_8_out, D);
  and and_25 (and_25_out, and_10_out, and_5_out);
  and and_26 (and_26_out, and_12_out, D);
  and and_27 (and_27_out, and_3_out, not_3_out);
  and and_28 (and_28_out, and_1_out, D);
  and and_29 (and_29_out, and_1_out, C);
  and and_30 (and_30_out, and_13_out, D);
  and and_31 (and_31_out, and_1_out, not_3_out);
  and and_32 (and_32_out, and_3_out, and_6_out);
  and and_33 (and_33_out, and_7_out, and_4_out);
  or or_1 (or_1_out, and_14_out, and_15_out);
  or or_2 (or_2_out, and_16_out, and_17_out);
  or or_3 (or_3_out, and_18_out, and_19_out);
  or or_4 (or_4_out, and_20_out, and_21_out);
  or or_5 (or_5_out, and_21_out, and_22_out);
  or or_6 (or_6_out, and_24_out, and_25_out);
  or or_7 (or_7_out, and_11_out, and_26_out);
  or or_8 (or_8_out, and_28_out, and_29_out);
  or or_9 (or_9_out, and_30_out, and_17_out);
  or or_10 (or_10_out, and_31_out, and_32_out);
  or or_11 (or_11_out, or_1_out, or_2_out);
  or or_12 (or_12_out, or_3_out, or_4_out);
  or or_13 (or_13_out, or_5_out, and_23_out);
  or or_14 (or_14_out, or_1_out, or_6_out);
  or or_15 (or_15_out, or_7_out, and_27_out);
  or or_16 (or_16_out, or_8_out, or_9_out);
  or or_17 (or_17_out, or_10_out, and_33_out);
  not not_5 (a_2, or_11_out);
  not not_6 (b_2, or_12_out);
  not not_7 (c_2, or_13_out);
  not not_8 (d_2, or_14_out);
  not not_9 (e, or_15_out);
  not not_10 (f, or_16_out);
  not not_11 (g, or_17_out);
endmodule

module BCH_test (
  input  A,
  input  B,
  input  C,
  input  D,
  input  in_5,
  input  in_6,
  input  in_7,
  input  in_8,
  input  in_9,
  input  in_10,
  input  in_11
);

  wire and_1_out, and_2_out, and_3_out, and_4_out, and_5_out, and_6_out, and_7_out, and_8_out, and_9_out,
       and_10_out, and_11_out, and_12_out, and_13_out, and_14_out, and_15_out, and_16_out, and_17_out,
       and_18_out, and_19_out, and_20_out, and_21_out, and_22_out, and_23_out, and_24_out, and_25_out,
       and_26_out, and_27_out, and_28_out, and_29_out, and_30_out, and_31_out, and_32_out, and_33_out,
       not_1_out, not_2_out, not_3_out, not_4_out, not_5_out, not_6_out, not_7_out, not_8_out, not_9_out,
       not_10_out, not_11_out, or_1_out, or_2_out, or_3_out, or_4_out, or_5_out, or_6_out, or_7_out,
       or_8_out, or_9_out, or_10_out, or_11_out, or_12_out, or_13_out, or_14_out, or_15_out, or_16_out,
       or_17_out;

  not not_1 (not_1_out, A);
  not not_2 (not_2_out, B);
  not not_3 (not_3_out, C);
  not not_4 (not_4_out, D);
  and and_1 (and_1_out, not_1_out, not_2_out);
  and and_2 (and_2_out, not_3_out, D);
  and and_3 (and_3_out, not_1_out, B);
  and and_4 (and_4_out, not_3_out, not_4_out);
  and and_5 (and_5_out, A, not_2_out);
  and and_6 (and_6_out, C, D);
  and and_7 (and_7_out, A, B);
  and and_8 (and_8_out, B, C);
  and and_9 (and_9_out, A, C);
  and and_10 (and_10_out, C, not_4_out);
  and and_11 (and_11_out, not_1_out, D);
  and and_12 (and_12_out, not_2_out, not_3_out);
  and and_13 (and_13_out, not_1_out, C);
  and and_14 (and_14_out, and_1_out, and_2_out);
  and and_15 (and_15_out, and_3_out, and_4_out);
  and and_16 (and_16_out, and_5_out, and_6_out);
  and and_17 (and_17_out, and_7_out, and_2_out);
  and and_18 (and_18_out, and_3_out, and_2_out);
  and and_19 (and_19_out, and_8_out, not_4_out);
  and and_20 (and_20_out, and_9_out, D);
  and and_21 (and_21_out, and_7_out, not_4_out);
  and and_22 (and_22_out, and_1_out, and_10_out);
  and and_23 (and_23_out, and_7_out, C);
  and and_24 (and_24_out, and_8_out, D);
  and and_25 (and_25_out, and_10_out, and_5_out);
  and and_26 (and_26_out, and_12_out, D);
  and and_27 (and_27_out, and_3_out, not_3_out);
  and and_28 (and_28_out, and_1_out, D);
  and and_29 (and_29_out, and_1_out, C);
  and and_30 (and_30_out, and_13_out, D);
  and and_31 (and_31_out, and_1_out, not_3_out);
  and and_32 (and_32_out, and_3_out, and_6_out);
  and and_33 (and_33_out, and_7_out, and_4_out);
  or or_1 (or_1_out, and_14_out, and_15_out);
  or or_2 (or_2_out, and_16_out, and_17_out);
  or or_3 (or_3_out, and_18_out, and_19_out);
  or or_4 (or_4_out, and_20_out, and_21_out);
  or or_5 (or_5_out, and_21_out, and_22_out);
  or or_6 (or_6_out, and_24_out, and_25_out);
  or or_7 (or_7_out, and_11_out, and_26_out);
  or or_8 (or_8_out, and_28_out, and_29_out);
  or or_9 (or_9_out, and_30_out, and_17_out);
  or or_10 (or_10_out, and_31_out, and_32_out);
  or or_11 (or_11_out, or_1_out, or_2_out);
  or or_12 (or_12_out, or_3_out, or_4_out);
  or or_13 (or_13_out, or_5_out, and_23_out);
  or or_14 (or_14_out, or_1_out, or_6_out);
  or or_15 (or_15_out, or_7_out, and_27_out);
  or or_16 (or_16_out, or_8_out, or_9_out);
  or or_17 (or_17_out, or_10_out, and_33_out);
  not not_5 (not_5_out, or_11_out);
  not not_6 (not_6_out, or_12_out);
  not not_7 (not_7_out, or_13_out);
  not not_8 (not_8_out, or_14_out);
  not not_9 (not_9_out, or_15_out);
  not not_10 (not_10_out, or_16_out);
  not not_11 (not_11_out, or_17_out);
  _7_Segment_Display u_7_segment_display_1 (
    .g(not_11_out), .f(not_10_out), .a(not_5_out), .b(not_6_out), .e(not_9_out), .d(not_8_out), .c(not_7_out));  // open: dp
  _7_Segment_Display u_7_segment_display_2 (
    .g(in_11), .f(in_10), .a(in_5), .b(in_6), .e(in_9), .d(in_8), .c(in_7));  // open: dp

  // Notes on the sheet:
  //   a
  //   b
  //   c
  //   d
  //   e
  //   f
  //   g
endmodule
