// Logisim project CECS361_RISC_CPU_Design.circ as structural Verilog: 1 circuit, main circuit main
module main (
  input  Load,
  input  Clear,
  input  Up_Down,
  input  Enable,
  input  in_5,
  input  in_6,
  input  in_7,
  input  in_8,
  input  in_9,
  input  in_10,
  input  in_11
);

  wire and_1_out, and_2_out, and_3_out, and_4_out, BT_Reg_Addr_out, clock_1_out, comparator_1_gt,
       comparator_2_gt, comparator_3_eq, comparator_3_lt, decoder_1_out0, decoder_1_out1, decoder_1_out2,
       decoder_1_out3, decoder_1_out4, decoder_1_out5, decoder_1_out6, decoder_1_out7, decoder_1_out8,
       decoder_1_out9, decoder_2_out0, decoder_2_out1, decoder_2_out2, decoder_2_out3, decoder_2_out4,
       decoder_2_out5, decoder_2_out6, decoder_2_out7, decoder_3_out0, decoder_3_out1, decoder_3_out2,
       decoder_3_out3, decoder_3_out4, decoder_3_out5, decoder_3_out6, decoder_3_out7, LED_Reg_Addr_out,
       not_1_out, not_2_out, not_3_out, not_4_out, not_5_out, not_6_out, not_7_out, not_8_out, not_9_out,
       not_10_out, not_11_out, not_12_out, not_13_out, not_14_out, not_15_out, not_16_out, not_17_out,
       not_18_out, not_19_out, not_20_out, not_21_out, not_22_out, not_23_out, not_24_out, not_25_out,
       or_1_out, priority_encoder_2_out, RGB_Reg_Addr_out, Seg_0_Addr_out, Seg_1_Addr_out, Seg_2_Addr_out,
       Seg_3_Addr_out, Seg_4_Addr_out, Seg_5_Addr_out, Seg_6_Addr_out, Seg_7_Addr_out, SW_Reg_Addr_out,
       undriven_4, undriven_6, undriven_7, undriven_8, undriven_9, undriven_10, undriven_11, undriven_12,
       undriven_13, undriven_14, undriven_15, undriven_16, xor_1_out;
  wire [2:0] demultiplexer_5_out3, demultiplexer_5_out4, demultiplexer_5_out5, demultiplexer_5_out6,
       demultiplexer_5_out7, demultiplexer_7_out2, demultiplexer_7_out3, demultiplexer_7_out4,
       demultiplexer_7_out5, demultiplexer_7_out6, demultiplexer_7_out7, demultiplexer_8_out0,
       demultiplexer_8_out1, demultiplexer_8_out8, demultiplexer_8_out9, demultiplexer_8_out10,
       demultiplexer_8_out11, demultiplexer_9_out8, demultiplexer_9_out9, demultiplexer_9_out10,
       demultiplexer_9_out11, multiplexer_5_out, multiplexer_7_out, undriven, undriven_2;
  wire [3:0] multiplexer_9_out, priority_encoder_1_out;
  wire [4:0] Right_out;
  wire [7:0] demultiplexer_11_out1;
  wire [11:0] multiplexer_1_out;
  wire [15:0] adder_1_out, and_5_out, BT_Reg_q, demultiplexer_1_out0, demultiplexer_1_out1,
       demultiplexer_1_out2, demultiplexer_1_out3, demultiplexer_1_out4, demultiplexer_1_out5,
       demultiplexer_1_out6, demultiplexer_1_out7, demultiplexer_2_out0, demultiplexer_2_out1,
       demultiplexer_2_out2, demultiplexer_2_out3, demultiplexer_2_out4, demultiplexer_2_out5,
       demultiplexer_2_out6, demultiplexer_2_out7, demultiplexer_2_out8, demultiplexer_2_out9,
       demultiplexer_3_out1, demultiplexer_4_out3, demultiplexer_4_out4, demultiplexer_4_out5,
       demultiplexer_4_out6, demultiplexer_4_out7, demultiplexer_6_out2, demultiplexer_6_out3,
       demultiplexer_6_out4, demultiplexer_6_out5, demultiplexer_6_out6, demultiplexer_6_out7,
       demultiplexer_10_out0, demultiplexer_10_out1, demultiplexer_11_out0, demultiplexer_11_out2,
       demultiplexer_11_out8, demultiplexer_11_out9, demultiplexer_11_out10, demultiplexer_11_out11,
       LED_Reg_q, multiplexer_2_out, multiplexer_3_out, multiplexer_4_out, multiplexer_6_out,
       multiplexer_8_out, multiplexer_10_out, or_2_out, Program_Counter_q, R0_q, R1_q, R2_q, R3_q, R4_q,
       R5_q, R6_q, R7_q, ram_1_dout, RGB_Reg_q, rom_1_data, Seg0_q, Seg1_q, Seg2_q, Seg3_q, Seg4_q, Seg5_q,
       Seg6_q, Seg7_q, subtractor_1_out, SW_Reg_q, undriven_3, undriven_5;
  wire [15:8] demultiplexer_11_out1_2;

  Clock #(.phaseOffset(1)) clock_1 (.out(clock_1_out));
  RAM #(.dataWidth(16)) ram_1 (
    .addr(demultiplexer_11_out1), .we(and_4_out), .oe(and_4_out), .clk(clock_1_out),
    .din(demultiplexer_10_out0), .dout(ram_1_dout));
  Multiplexer #(.select(4), .width(12)) multiplexer_1 (.out(multiplexer_1_out));  // open: in0, in1, in2, in3, in4, in5, in6, in7, in8, in9, in10, in11, in12, in13, in14, in15, sel
  Decoder #(.select(4)) decoder_1 (
    .out0(decoder_1_out0), .out1(decoder_1_out1), .out2(decoder_1_out2), .out3(decoder_1_out3),
    .out4(decoder_1_out4), .out5(decoder_1_out5), .out6(decoder_1_out6), .out7(decoder_1_out7),
    .out8(decoder_1_out8), .out9(decoder_1_out9), .sel(multiplexer_9_out), .en(and_4_out));  // open: out10, out11, out12, out13, out14, out15
  Decoder #(.select(3)) decoder_2 (
    .out0(decoder_2_out0), .out1(decoder_2_out1), .out2(decoder_2_out2), .out3(decoder_2_out3),
    .out4(decoder_2_out4), .out5(decoder_2_out5), .out6(decoder_2_out6), .out7(decoder_2_out7));  // open: sel, en
  Decoder #(.select(3)) decoder_3 (
    .out0(decoder_3_out0), .out1(decoder_3_out1), .out2(decoder_3_out2), .out3(decoder_3_out3),
    .out4(decoder_3_out4), .out5(decoder_3_out5), .out6(decoder_3_out6), .out7(decoder_3_out7),
    .sel(multiplexer_7_out), .en(and_2_out));
  Multiplexer #(.width(16)) multiplexer_2 (
    .in0(SW_Reg_q), .in1(BT_Reg_q), .out(multiplexer_2_out), .sel(priority_encoder_2_out));
  Multiplexer #(.select(3), .width(16)) multiplexer_3 (
    .in0(R0_q), .in1(R1_q), .in2(R2_q), .in3(R3_q), .in4(R4_q), .in5(R5_q), .in6(R6_q), .in7(R7_q),
    .out(multiplexer_3_out), .sel(undriven));
  Multiplexer #(.select(3), .width(16)) multiplexer_4 (
    .in0(R0_q), .in1(R1_q), .in2(R2_q), .in3(R3_q), .in4(R4_q), .in5(R5_q), .in6(R6_q), .in7(R7_q),
    .out(multiplexer_4_out), .sel(undriven_2));
  Demultiplexer #(.select(3), .width(16)) demultiplexer_1 (
    .out0(demultiplexer_1_out0), .out1(demultiplexer_1_out1), .out2(demultiplexer_1_out2),
    .out3(demultiplexer_1_out3), .out4(demultiplexer_1_out4), .out5(demultiplexer_1_out5),
    .out6(demultiplexer_1_out6), .out7(demultiplexer_1_out7), .in(multiplexer_6_out), .sel(multiplexer_5_out));
  Demultiplexer #(.select(4), .width(16)) demultiplexer_2 (
    .out0(demultiplexer_2_out0), .out1(demultiplexer_2_out1), .out2(demultiplexer_2_out2),
    .out3(demultiplexer_2_out3), .out4(demultiplexer_2_out4), .out5(demultiplexer_2_out5),
    .out6(demultiplexer_2_out6), .out7(demultiplexer_2_out7), .out8(demultiplexer_2_out8),
    .out9(demultiplexer_2_out9), .in(multiplexer_8_out), .sel(priority_encoder_1_out));  // open: out10, out11, out12, out13, out14, out15
  Register #(.width(16)) R7 (
    .D(demultiplexer_1_out7), .en(decoder_3_out7), .clk(clock_1_out), .Q(R7_q), .clr(decoder_2_out7));
  Demultiplexer #(.select(4), .width(16)) demultiplexer_3 (
    .out1(demultiplexer_3_out1), .in(multiplexer_2_out), .sel(rom_1_data[15:12]));  // open: out0, out2, out3, out4, out5, out6, out7, out8, out9, out10, out11, out12, out13, out14, out15
  Counter #(.max('hffff), .width(16)) Program_Counter (
    .clr(Clear), .load(and_1_out), .up(Up_Down), .count(Enable), .clk(clock_1_out),
    .D({4'b0000, multiplexer_1_out}), .Q(Program_Counter_q));  // open: carry
  Demultiplexer #(.select(4), .width(16)) demultiplexer_4 (
    .out3(demultiplexer_4_out3), .out4(demultiplexer_4_out4), .out5(demultiplexer_4_out5),
    .out6(demultiplexer_4_out6), .out7(demultiplexer_4_out7), .in(multiplexer_3_out), .sel(rom_1_data[15:12]));  // open: out0, out1, out2, out8, out9, out10, out11, out12, out13, out14, out15
  ROM #(.dataWidth(16)) rom_1 (.addr(Program_Counter_q[7:0]), .data(rom_1_data));
  Register #(.width(16)) R6 (
    .D(demultiplexer_1_out6), .en(decoder_3_out6), .clk(clock_1_out), .Q(R6_q), .clr(decoder_2_out6));
  Demultiplexer #(.select(4), .width(3)) demultiplexer_5 (
    .out3(demultiplexer_5_out3), .out4(demultiplexer_5_out4), .out5(demultiplexer_5_out5),
    .out6(demultiplexer_5_out6), .out7(demultiplexer_5_out7), .in(undriven), .sel(rom_1_data[15:12]));  // open: out0, out1, out2, out8, out9, out10, out11, out12, out13, out14, out15
  Demultiplexer #(.select(4), .width(16)) demultiplexer_6 (
    .out2(demultiplexer_6_out2), .out3(demultiplexer_6_out3), .out4(demultiplexer_6_out4),
    .out5(demultiplexer_6_out5), .out6(demultiplexer_6_out6), .out7(demultiplexer_6_out7),
    .in(multiplexer_4_out), .sel(rom_1_data[15:12]));  // open: out0, out1, out8, out9, out10, out11, out12, out13, out14, out15
  and and_1 (and_1_out, rom_1_data[15], not_1_out);
  not not_1 (not_1_out, rom_1_data[14]);
  Demultiplexer #(.select(4), .width(3)) demultiplexer_7 (
    .out2(demultiplexer_7_out2), .out3(demultiplexer_7_out3), .out4(demultiplexer_7_out4),
    .out5(demultiplexer_7_out5), .out6(demultiplexer_7_out6), .out7(demultiplexer_7_out7), .in(undriven_2),
    .sel(rom_1_data[15:12]));  // open: out0, out1, out8, out9, out10, out11, out12, out13, out14, out15
  Register #(.width(16)) R5 (
    .D(demultiplexer_1_out5), .en(decoder_3_out5), .clk(clock_1_out), .Q(R5_q), .clr(decoder_2_out5));
  Demultiplexer #(.select(4), .width(3)) demultiplexer_8 (
    .out0(demultiplexer_8_out0), .out1(demultiplexer_8_out1), .out2(demultiplexer_7_out2),
    .out3(demultiplexer_7_out3), .out4(demultiplexer_7_out4), .out5(demultiplexer_7_out5),
    .out6(demultiplexer_7_out6), .out7(demultiplexer_7_out7), .out8(demultiplexer_8_out8),
    .out9(demultiplexer_8_out9), .out10(demultiplexer_8_out10), .out11(demultiplexer_8_out11),
    .in(rom_1_data[11:9]), .sel(rom_1_data[15:12]));  // open: out12, out13, out14, out15
  Multiplexer #(.select(4), .width(3)) multiplexer_5 (
    .in0(demultiplexer_8_out0), .in1(demultiplexer_8_out1), .in2(demultiplexer_7_out2),
    .in3(demultiplexer_7_out3), .in4(demultiplexer_7_out4), .in5(demultiplexer_7_out5),
    .in6(demultiplexer_7_out6), .in7(demultiplexer_7_out7), .out(multiplexer_5_out), .sel(rom_1_data[15:12]));  // open: in8, in9, in10, in11, in12, in13, in14, in15
  Multiplexer #(.select(4), .width(16)) multiplexer_6 (
    .in0(demultiplexer_11_out0), .in1(multiplexer_10_out), .in2(undriven_3), .in3(adder_1_out),
    .in4(subtractor_1_out), .in5(and_5_out), .in6(or_2_out), .out(multiplexer_6_out), .sel(rom_1_data[15:12]));  // open: in7, in8, in9, in10, in11, in12, in13, in14, in15
  Multiplexer #(.select(4), .width(3)) multiplexer_7 (
    .in0(demultiplexer_8_out0), .in1(demultiplexer_8_out1), .in2(demultiplexer_7_out2),
    .out(multiplexer_7_out), .sel(rom_1_data[15:12]));  // open: in3, in4, in5, in6, in7, in8, in9, in10, in11, in12, in13, in14, in15
  Multiplexer #(.select(4), .width(16)) multiplexer_8 (
    .in2(demultiplexer_10_out1), .out(multiplexer_8_out), .sel(rom_1_data[15:12]));  // open: in0, in1, in3, in4, in5, in6, in7, in8, in9, in10, in11, in12, in13, in14, in15
  Multiplexer #(.select(4), .width(4)) multiplexer_9 (
    .in2(priority_encoder_1_out), .out(multiplexer_9_out), .sel(rom_1_data[15:12]));  // open: in0, in1, in3, in4, in5, in6, in7, in8, in9, in10, in11, in12, in13, in14, in15
  Multiplexer #(.width(16)) multiplexer_10 (
    .in0(ram_1_dout), .in1(demultiplexer_3_out1), .out(multiplexer_10_out), .sel(comparator_1_gt));
  Register #(.width(16)) R4 (
    .D(demultiplexer_1_out4), .en(decoder_3_out4), .clk(clock_1_out), .Q(R4_q), .clr(decoder_2_out4));
  Demultiplexer #(.select(4), .width(3)) demultiplexer_9 (
    .out3(demultiplexer_5_out3), .out4(demultiplexer_5_out4), .out5(demultiplexer_5_out5),
    .out6(demultiplexer_5_out6), .out7(demultiplexer_5_out7), .out8(demultiplexer_9_out8),
    .out9(demultiplexer_9_out9), .out10(demultiplexer_9_out10), .out11(demultiplexer_9_out11),
    .in(rom_1_data[8:6]), .sel(rom_1_data[15:12]));  // open: out0, out1, out2, out12, out13, out14, out15
  Demultiplexer #(.width(16)) demultiplexer_10 (
    .out0(demultiplexer_10_out0), .out1(demultiplexer_10_out1), .in(demultiplexer_6_out2),
    .sel(comparator_2_gt));
  not not_2 (not_2_out, rom_1_data[15]);
  not not_3 (not_3_out, rom_1_data[13]);
  or or_1 (or_1_out, rom_1_data[14], not_3_out, rom_1_data[12]);
  and and_2 (and_2_out, not_2_out, or_1_out);
  not not_4 (not_4_out, rom_1_data[15]);
  not not_5 (not_5_out, rom_1_data[14]);
  and and_3 (and_3_out, not_4_out, not_5_out);
  and and_4 (and_4_out, and_3_out, xor_1_out);
  Register #(.width(16)) R3 (
    .D(demultiplexer_1_out3), .en(decoder_3_out3), .clk(clock_1_out), .Q(R3_q), .clr(decoder_2_out3));
  xor xor_1 (xor_1_out, rom_1_data[13], rom_1_data[12]);
  Comparator #(.width(16)) comparator_1 (
    .a({demultiplexer_11_out1_2, demultiplexer_11_out1}),
    .b({{10{1'b0}}, in_6, in_7, in_8, in_9, in_10, in_11}), .gt(comparator_1_gt));  // open: eq, lt
  Comparator #(.width(16)) comparator_2 (
    .a(demultiplexer_11_out2), .b({{10{1'b0}}, in_6, in_7, in_8, in_9, in_10, in_11}), .gt(comparator_2_gt));  // open: eq, lt
  Demultiplexer #(.select(4), .width(16)) demultiplexer_11 (
    .out0(demultiplexer_11_out0), .out1({demultiplexer_11_out1_2, demultiplexer_11_out1}),
    .out2(demultiplexer_11_out2), .out8(demultiplexer_11_out8), .out9(demultiplexer_11_out9),
    .out10(demultiplexer_11_out10), .out11(demultiplexer_11_out11), .in({{10{1'b0}}, rom_1_data[5:0]}),
    .sel(rom_1_data[15:12]));  // open: out3, out4, out5, out6, out7, out12, out13, out14, out15
  not not_6 (not_6_out, rom_1_data[3]);
  not not_7 (not_7_out, rom_1_data[1]);
  and BT_Reg_Addr (BT_Reg_Addr_out, rom_1_data[5], rom_1_data[4], not_6_out, rom_1_data[2], not_7_out, not_8_out);
  Register #(.width(16)) R2 (
    .D(demultiplexer_1_out2), .en(decoder_3_out2), .clk(clock_1_out), .Q(R2_q), .clr(decoder_2_out2));
  not not_8 (not_8_out, rom_1_data[0]);
  not not_9 (not_9_out, rom_1_data[3]);
  not not_10 (not_10_out, rom_1_data[1]);
  and SW_Reg_Addr (SW_Reg_Addr_out, rom_1_data[5], rom_1_data[4], not_9_out, rom_1_data[2], not_10_out, rom_1_data[0]);
  not not_11 (not_11_out, rom_1_data[3]);
  and LED_Reg_Addr (LED_Reg_Addr_out, rom_1_data[5], rom_1_data[4], not_11_out, rom_1_data[2], rom_1_data[1], not_12_out);
  not not_12 (not_12_out, rom_1_data[0]);
  not not_13 (not_13_out, rom_1_data[3]);
  and RGB_Reg_Addr (RGB_Reg_Addr_out, rom_1_data[5], rom_1_data[4], not_13_out, rom_1_data[2], rom_1_data[1], rom_1_data[0]);
  not not_14 (not_14_out, rom_1_data[0]);
  not not_15 (not_15_out, rom_1_data[1]);
  not not_16 (not_16_out, rom_1_data[2]);
  and Seg_7_Addr (Seg_7_Addr_out, rom_1_data[5], rom_1_data[4], rom_1_data[3], not_16_out, not_15_out, not_14_out);
  Register #(.width(16)) R1 (
    .D(demultiplexer_1_out1), .en(decoder_3_out1), .clk(clock_1_out), .Q(R1_q), .clr(decoder_2_out1));
  not not_17 (not_17_out, rom_1_data[1]);
  not not_18 (not_18_out, rom_1_data[2]);
  and Seg_6_Addr (Seg_6_Addr_out, rom_1_data[5], rom_1_data[4], rom_1_data[3], not_18_out, not_17_out, rom_1_data[0]);
  not not_19 (not_19_out, rom_1_data[0]);
  not not_20 (not_20_out, rom_1_data[2]);
  and Seg_5_Addr (Seg_5_Addr_out, rom_1_data[5], rom_1_data[4], rom_1_data[3], not_20_out, rom_1_data[1], not_19_out);
  not not_21 (not_21_out, rom_1_data[2]);
  and Seg_4_Addr (Seg_4_Addr_out, rom_1_data[5], rom_1_data[4], rom_1_data[3], not_21_out, rom_1_data[1], rom_1_data[0]);
  not not_22 (not_22_out, rom_1_data[1]);
  and Seg_3_Addr (Seg_3_Addr_out, rom_1_data[5], rom_1_data[4], rom_1_data[3], rom_1_data[2], not_22_out, not_23_out);
  Button Left (.out(Right_out[2]));
  not not_23 (not_23_out, rom_1_data[0]);
  not not_24 (not_24_out, rom_1_data[1]);
  and Seg_2_Addr (Seg_2_Addr_out, rom_1_data[5], rom_1_data[4], rom_1_data[3], rom_1_data[2], not_24_out, rom_1_data[0]);
  Button Up (.out(Right_out[3]));
  Button Enter (.out(Right_out[4]));
  Button Down (.out(Right_out[1]));
  and Seg_1_Addr (Seg_1_Addr_out, rom_1_data[5], rom_1_data[4], rom_1_data[3], rom_1_data[2], rom_1_data[1], not_25_out);
  Register #(.width(16)) R0 (
    .D(demultiplexer_1_out0), .en(decoder_3_out0), .clk(clock_1_out), .Q(R0_q), .clr(decoder_2_out0));
  // DipSwitch #(.number(16)) dipswitch_1: pin names not known
  Button Right (.out(Right_out[0]));
  not not_25 (not_25_out, rom_1_data[0]);
  and Seg_0_Addr (Seg_0_Addr_out, rom_1_data[5], rom_1_data[4], rom_1_data[3], rom_1_data[2], rom_1_data[1], rom_1_data[0]);
  // RGBLED RGB: pin names not known
  Priority_Encoder #(.select(4)) priority_encoder_1 (
    .in0(Seg_0_Addr_out), .in1(Seg_1_Addr_out), .in2(Seg_2_Addr_out), .in3(Seg_3_Addr_out),
    .in4(Seg_4_Addr_out), .in5(Seg_5_Addr_out), .in6(Seg_6_Addr_out), .in7(Seg_7_Addr_out),
    .in8(RGB_Reg_Addr_out), .in9(LED_Reg_Addr_out), .out(priority_encoder_1_out), .en_in(in_5));  // open: in10, in11, in12, in13, in14, in15, gs, en_out
  Priority_Encoder #(.select(1)) priority_encoder_2 (
    .in0(SW_Reg_Addr_out), .in1(BT_Reg_Addr_out), .out(priority_encoder_2_out), .en_in(in_5));  // open: gs, en_out
  Register #(.width(16)) BT_Reg (
    .D({{11{1'b0}}, Right_out}), .en(1'b1), .clk(clock_1_out), .Q(BT_Reg_q), .clr(undriven_4));
  // LedBar #(.inputtype("row"), .matrixcols(16)) ledbar_1: pin names not known
  Register #(.width(16)) SW_Reg (.D(undriven_5), .en(1'b1), .clk(clock_1_out), .Q(SW_Reg_q), .clr(undriven_6));
  _7_Segment_Display u_7_segment_display_1 (
    .g(Seg7_q[6]), .f(Seg7_q[5]), .a(Seg7_q[0]), .b(Seg7_q[1]), .e(Seg7_q[4]), .d(Seg7_q[3]), .c(Seg7_q[2]));  // open: dp
  Register #(.width(16)) LED_Reg (
    .D(demultiplexer_2_out9), .en(decoder_1_out9), .clk(clock_1_out), .Q(LED_Reg_q), .clr(undriven_7));
  _7_Segment_Display u_7_segment_display_2 (
    .g(Seg6_q[6]), .f(Seg6_q[5]), .a(Seg6_q[0]), .b(Seg6_q[1]), .e(Seg6_q[4]), .d(Seg6_q[3]), .c(Seg6_q[2]));  // open: dp
  _7_Segment_Display u_7_segment_display_3 (
    .g(Seg5_q[6]), .f(Seg5_q[5]), .a(Seg5_q[0]), .b(Seg5_q[1]), .e(Seg5_q[4]), .d(Seg5_q[3]), .c(Seg5_q[2]));  // open: dp
  _7_Segment_Display u_7_segment_display_4 (
    .g(Seg4_q[6]), .f(Seg4_q[5]), .a(Seg4_q[0]), .b(Seg4_q[1]), .e(Seg4_q[4]), .d(Seg4_q[3]), .c(Seg4_q[2]));  // open: dp
  _7_Segment_Display u_7_segment_display_5 (
    .g(Seg3_q[6]), .f(Seg3_q[5]), .a(Seg3_q[0]), .b(Seg3_q[1]), .e(Seg3_q[4]), .d(Seg3_q[3]), .c(Seg3_q[2]));  // open: dp
  Register #(.width(16)) RGB_Reg (
    .D(demultiplexer_2_out8), .en(decoder_1_out8), .clk(clock_1_out), .Q(RGB_Reg_q), .clr(undriven_8));
  _7_Segment_Display u_7_segment_display_6 (
    .g(Seg2_q[6]), .f(Seg2_q[5]), .a(Seg2_q[0]), .b(Seg2_q[1]), .e(Seg2_q[4]), .d(Seg2_q[3]), .c(Seg2_q[2]));  // open: dp
  Register #(.width(16)) Seg7 (
    .D(demultiplexer_2_out7), .en(decoder_1_out7), .clk(clock_1_out), .Q(Seg7_q), .clr(undriven_9));
  _7_Segment_Display u_7_segment_display_7 (
    .g(Seg1_q[6]), .f(Seg1_q[5]), .a(Seg1_q[0]), .b(Seg1_q[1]), .e(Seg1_q[4]), .d(Seg1_q[3]), .c(Seg1_q[2]));  // open: dp
  _7_Segment_Display u_7_segment_display_8 (
    .g(Seg0_q[6]), .f(Seg0_q[5]), .a(Seg0_q[0]), .b(Seg0_q[1]), .e(Seg0_q[4]), .d(Seg0_q[3]), .c(Seg0_q[2]));  // open: dp
  Register #(.width(16)) Seg6 (
    .D(demultiplexer_2_out6), .en(decoder_1_out6), .clk(clock_1_out), .Q(Seg6_q), .clr(undriven_10));
  Register #(.width(16)) Seg5 (
    .D(demultiplexer_2_out5), .en(decoder_1_out5), .clk(clock_1_out), .Q(Seg5_q), .clr(undriven_11));
  Register #(.width(16)) Seg4 (
    .D(demultiplexer_2_out4), .en(decoder_1_out4), .clk(clock_1_out), .Q(Seg4_q), .clr(undriven_12));
  Register #(.width(16)) Seg3 (
    .D(demultiplexer_2_out3), .en(decoder_1_out3), .clk(clock_1_out), .Q(Seg3_q), .clr(undriven_13));
  Register #(.width(16)) Seg2 (
    .D(demultiplexer_2_out2), .en(decoder_1_out2), .clk(clock_1_out), .Q(Seg2_q), .clr(undriven_14));
  Register #(.width(16)) Seg1 (
    .D(demultiplexer_2_out1), .en(decoder_1_out1), .clk(clock_1_out), .Q(Seg1_q), .clr(undriven_15));
  Register #(.width(16)) Seg0 (
    .D(demultiplexer_2_out0), .en(decoder_1_out0), .clk(clock_1_out), .Q(Seg0_q), .clr(undriven_16));
  Adder #(.width(16)) adder_1 (
    .a(demultiplexer_6_out3), .b(demultiplexer_4_out3), .out(adder_1_out));  // open: cin, cout
  Subtractor #(.width(16)) subtractor_1 (
    .a(demultiplexer_6_out4), .b(demultiplexer_4_out4), .out(subtractor_1_out));  // open: bin, bout
  assign and_5_out = demultiplexer_6_out5 & demultiplexer_4_out5;  // AND_Gate and_5, 16 bits wide
  assign or_2_out = demultiplexer_6_out6 | demultiplexer_4_out6;  // OR_Gate or_2, 16 bits wide
  Comparator #(.width(16)) comparator_3 (
    .a(demultiplexer_6_out7), .b(demultiplexer_4_out7), .eq(comparator_3_eq), .lt(comparator_3_lt));  // open: gt

  // Notes on the sheet:
  //   contents of rom_1 (hex, n*v repeats v):
  //   fff 1fff 2fff 3fff 4fff 5fff 6fff 7fff 8fff 9fff afff bfff cfff dfff efff fddd 28b 28a 289 288 287
  //   286 285 284 293 282 281 280 0 e3f 0 3f
endmodule
